// Logisim project micro.circ as structural Verilog: 1 circuit, main circuit EV20_Superescalar
module EV20_Superescalar (
  input  in_1
);

  wire ALU_is_done, ALU_is_free, ALUALULAU_cyout, and_1_out, and_2_out, and_3_out, and_4_out,
       bloque1_bsr_1_preload, bloque1_jmp_1_preload, CLK, CLK2, CLK3, CLK4, CYin, HOLD, LatchMemEnable,
       MEM_is_done, mem_is_free, nor_1_out, not_1_out, not_2_out, not_3_out, not_4_out, or_1_out, or_2_out,
       or_3_out, or_4_out, pipeline_register_viewer_1_a_is_enabled, pipeline_register_viewer_1_b_is_enabled,
       pipeline_register_viewer_1_c_is_enabled, pipeline_register_viewer_2_a_is_enabled,
       pipeline_register_viewer_2_b_is_enabled, pipeline_register_viewer_2_c_is_enabled,
       pipeline_register_viewer_3_a_is_enabled, pipeline_register_viewer_3_b_is_enabled,
       pipeline_register_viewer_3_c_is_enabled, pipeline_register_viewer_4_a_is_enabled,
       pipeline_register_viewer_4_b_is_enabled, pipeline_register_viewer_4_c_is_enabled, register_1_q,
       register_2_q, register_bank_viewer_1_a_is_enabled, register_bank_viewer_1_b_is_enabled,
       register_bank_viewer_1_c_is_enabled, uc1_1_p5, uc1_1_p6, UC1_HOLD, undriven, undriven_2, undriven_3,
       undriven_5, undriven_8;
  wire [1:0] ALU_Pipeline_sh_out, MREtapa2Pipeline, MRMW, pipeline_register_1_mrymw_out,
       pipeline_register_1_sh_out, undriven_4;
  wire [2:0] ProgramCounterReg_pc_2;
  wire [3:0] ALU_Pipeline_aluc_out, output_ports_viewer_1_hex_disp_0_0, output_ports_viewer_1_hex_disp_0_1,
       output_ports_viewer_1_hex_disp_0_2, output_ports_viewer_1_hex_disp_0_3,
       output_ports_viewer_1_hex_disp_1_0, output_ports_viewer_1_hex_disp_1_1,
       output_ports_viewer_1_hex_disp_1_2, output_ports_viewer_1_hex_disp_1_3, pipeline_register_1_aluc_out,
       pipeline_register_viewer_1_a_lsn, pipeline_register_viewer_1_a_msn, pipeline_register_viewer_1_b0,
       pipeline_register_viewer_1_b1, pipeline_register_viewer_1_b2, pipeline_register_viewer_1_b3,
       pipeline_register_viewer_1_b4, pipeline_register_viewer_1_b5, pipeline_register_viewer_1_b6,
       pipeline_register_viewer_1_b7, pipeline_register_viewer_1_b8, pipeline_register_viewer_1_b9,
       pipeline_register_viewer_1_b10, pipeline_register_viewer_1_b11, pipeline_register_viewer_1_b12,
       pipeline_register_viewer_1_b13, pipeline_register_viewer_1_b14, pipeline_register_viewer_1_b15,
       pipeline_register_viewer_1_b16, pipeline_register_viewer_1_b_lsn, pipeline_register_viewer_1_b_msn,
       pipeline_register_viewer_1_c_lsn, pipeline_register_viewer_1_c_msn, pipeline_register_viewer_2_a_lsn,
       pipeline_register_viewer_2_a_msn, pipeline_register_viewer_2_b0, pipeline_register_viewer_2_b1,
       pipeline_register_viewer_2_b2, pipeline_register_viewer_2_b3, pipeline_register_viewer_2_b4,
       pipeline_register_viewer_2_b5, pipeline_register_viewer_2_b6, pipeline_register_viewer_2_b7,
       pipeline_register_viewer_2_b8, pipeline_register_viewer_2_b9, pipeline_register_viewer_2_b10,
       pipeline_register_viewer_2_b11, pipeline_register_viewer_2_b12, pipeline_register_viewer_2_b13,
       pipeline_register_viewer_2_b14, pipeline_register_viewer_2_b15, pipeline_register_viewer_2_b16,
       pipeline_register_viewer_2_b_lsn, pipeline_register_viewer_2_b_msn, pipeline_register_viewer_2_c_lsn,
       pipeline_register_viewer_2_c_msn, pipeline_register_viewer_3_a_lsn, pipeline_register_viewer_3_a_msn,
       pipeline_register_viewer_3_b0, pipeline_register_viewer_3_b1, pipeline_register_viewer_3_b2,
       pipeline_register_viewer_3_b3, pipeline_register_viewer_3_b4, pipeline_register_viewer_3_b5,
       pipeline_register_viewer_3_b6, pipeline_register_viewer_3_b7, pipeline_register_viewer_3_b8,
       pipeline_register_viewer_3_b9, pipeline_register_viewer_3_b10, pipeline_register_viewer_3_b11,
       pipeline_register_viewer_3_b12, pipeline_register_viewer_3_b13, pipeline_register_viewer_3_b14,
       pipeline_register_viewer_3_b15, pipeline_register_viewer_3_b16, pipeline_register_viewer_3_b_lsn,
       pipeline_register_viewer_3_b_msn, pipeline_register_viewer_3_c_lsn, pipeline_register_viewer_3_c_msn,
       pipeline_register_viewer_4_a_lsn, pipeline_register_viewer_4_a_msn, pipeline_register_viewer_4_b0,
       pipeline_register_viewer_4_b1, pipeline_register_viewer_4_b2, pipeline_register_viewer_4_b3,
       pipeline_register_viewer_4_b4, pipeline_register_viewer_4_b5, pipeline_register_viewer_4_b6,
       pipeline_register_viewer_4_b7, pipeline_register_viewer_4_b8, pipeline_register_viewer_4_b9,
       pipeline_register_viewer_4_b10, pipeline_register_viewer_4_b11, pipeline_register_viewer_4_b12,
       pipeline_register_viewer_4_b13, pipeline_register_viewer_4_b14, pipeline_register_viewer_4_b15,
       pipeline_register_viewer_4_b16, pipeline_register_viewer_4_b_lsn, pipeline_register_viewer_4_b_msn,
       pipeline_register_viewer_4_c_lsn, pipeline_register_viewer_4_c_msn,
       register_bank_viewer_1_a_address_n0, register_bank_viewer_1_a_address_n1,
       register_bank_viewer_1_a_address_n2, register_bank_viewer_1_a_address_n3,
       register_bank_viewer_1_a_data_lsn, register_bank_viewer_1_a_data_msn,
       register_bank_viewer_1_b_address_n0, register_bank_viewer_1_b_address_n1,
       register_bank_viewer_1_b_address_n2, register_bank_viewer_1_b_address_n3,
       register_bank_viewer_1_b_data_lsn, register_bank_viewer_1_b_data_msn,
       register_bank_viewer_1_c_address_n0, register_bank_viewer_1_c_address_n1,
       register_bank_viewer_1_c_address_n2, register_bank_viewer_1_c_address_n3,
       register_bank_viewer_1_c_data_lsn, register_bank_viewer_1_c_data_msn;
  wire [5:0] A_Etapa1, ALU_Pipeline_a_bus_out, ALU_Pipeline_b_bus_out, ALU_Pipeline_t_bus_out, B_Etapa1,
       C_Etapa1, C_Etapa2Alu, C_Etapa2Mem, C_Etapa3, instruction2register_1_p3, instruction2register_1_p4,
       instruction2register_1_p5, judge_1_a_bus, judge_1_b_bus, judge_1_c_bus, LoadStore_a_bus_out,
       LoadStore_b_bus_out, pipeline_register_1_t_bus_out, pipeline_register_2_a_bus_out,
       pipeline_register_2_b_bus_out;
  wire [7:0] clk_edge_viewer_1_out_2, clk_edge_viewer_1_out_3, clk_edge_viewer_1_out_4,
       clk_edge_viewer_1_out_5, clk_edge_viewer_1_out_6, clk_edge_viewer_1_out_7, clk_edge_viewer_1_out_8,
       clk_edge_viewer_1_out_9, ProgramCounterReg_pc, uc2_viewer_1_out_2, uc2_viewer_1_out_3,
       uc2_viewer_1_out_4, uc2_viewer_1_out_5, uc2_viewer_1_out_6, uc2_viewer_1_out_7, uc2_viewer_1_out_8,
       uc2_viewer_1_out_9, uc2_viewer_2_out_2, uc2_viewer_2_out_3, uc2_viewer_2_out_4, uc2_viewer_2_out_5,
       uc2_viewer_2_out_6, uc2_viewer_2_out_7, uc2_viewer_2_out_8, uc2_viewer_2_out_9;
  wire [8:8] ALU_Pipeline_kmx_out, pipeline_register_1_kmx_out;
  wire [9:0] ALU_Pipeline_d_address_out, instruction2register_1_p2, LoadStore_d_address_out,
       pipeline_register_1_d_address_out, register_3_q;
  wire [10:0] bloque1_bsr_1_next_address;
  wire [14:0] judge_1_reg_out, LoadStore_t_bus_out, MicroInstructionROM_microinstruction,
       pipeline_register_2_t_bus_out;
  wire [15:0] ALU_RESULT, ALUALULAU_z, BusA_ALU_q, BusA_LS_q, BusB_ALU_q, Constant_K_q, data_1_datamemout,
       dipswitch_1_sw16, dipswitch_2_sw16, instruction2register_1_p6, multiplexer_1_out, reg_C_write,
       register_6_q, register_bank_1_register_out_a_data, register_bank_1_register_out_b_data,
       shiftersh_1_out_3, undriven_6, undriven_7;
  wire [23:0] BBUS, ProgramMemory_data;
  wire [31:0] output_ports_viewer_1_mat_0_col_0, output_ports_viewer_1_mat_0_col_0_2,
       output_ports_viewer_1_mat_0_col_0_3, output_ports_viewer_1_mat_0_col_0_4,
       output_ports_viewer_1_mat_0_col_0_5, output_ports_viewer_1_mat_0_col_0_6,
       output_ports_viewer_1_mat_0_col_0_7, output_ports_viewer_1_mat_0_col_0_8,
       output_ports_viewer_1_mat_0_col_1, output_ports_viewer_1_mat_0_col_1_2,
       output_ports_viewer_1_mat_0_col_1_3, output_ports_viewer_1_mat_0_col_1_4,
       output_ports_viewer_1_mat_0_col_1_5, output_ports_viewer_1_mat_0_col_1_6,
       output_ports_viewer_1_mat_0_col_1_7, output_ports_viewer_1_mat_0_col_1_8,
       output_ports_viewer_1_mat_0_col_2, output_ports_viewer_1_mat_0_col_2_2,
       output_ports_viewer_1_mat_0_col_2_3, output_ports_viewer_1_mat_0_col_2_4,
       output_ports_viewer_1_mat_0_col_2_5, output_ports_viewer_1_mat_0_col_2_6,
       output_ports_viewer_1_mat_0_col_2_7, output_ports_viewer_1_mat_0_col_2_8,
       output_ports_viewer_1_mat_0_col_3, output_ports_viewer_1_mat_0_col_3_2,
       output_ports_viewer_1_mat_0_col_3_3, output_ports_viewer_1_mat_0_col_3_4,
       output_ports_viewer_1_mat_0_col_3_5, output_ports_viewer_1_mat_0_col_3_6,
       output_ports_viewer_1_mat_0_col_3_7, output_ports_viewer_1_mat_0_col_3_8,
       output_ports_viewer_1_mat_1_col_0, output_ports_viewer_1_mat_1_col_0_2,
       output_ports_viewer_1_mat_1_col_0_3, output_ports_viewer_1_mat_1_col_0_4,
       output_ports_viewer_1_mat_1_col_0_5, output_ports_viewer_1_mat_1_col_0_6,
       output_ports_viewer_1_mat_1_col_0_7, output_ports_viewer_1_mat_1_col_0_8,
       output_ports_viewer_1_mat_1_col_1, output_ports_viewer_1_mat_1_col_1_2,
       output_ports_viewer_1_mat_1_col_1_3, output_ports_viewer_1_mat_1_col_1_4,
       output_ports_viewer_1_mat_1_col_1_5, output_ports_viewer_1_mat_1_col_1_6,
       output_ports_viewer_1_mat_1_col_1_7, output_ports_viewer_1_mat_1_col_1_8,
       output_ports_viewer_1_mat_1_col_2, output_ports_viewer_1_mat_1_col_2_2,
       output_ports_viewer_1_mat_1_col_2_3, output_ports_viewer_1_mat_1_col_2_4,
       output_ports_viewer_1_mat_1_col_2_5, output_ports_viewer_1_mat_1_col_2_6,
       output_ports_viewer_1_mat_1_col_2_7, output_ports_viewer_1_mat_1_col_2_8,
       output_ports_viewer_1_mat_1_col_3, output_ports_viewer_1_mat_1_col_3_2,
       output_ports_viewer_1_mat_1_col_3_3, output_ports_viewer_1_mat_1_col_3_4,
       output_ports_viewer_1_mat_1_col_3_5, output_ports_viewer_1_mat_1_col_3_6,
       output_ports_viewer_1_mat_1_col_3_7, output_ports_viewer_1_mat_1_col_3_8;

  Hex_Digit_Display hex_digit_display_1 (.value({1'b0, ProgramCounterReg_pc_2}));  // open: dp
  // Probe on {ProgramCounterReg_pc_2, ProgramCounterReg_pc}
  ROM #(.addrWidth(11), .dataWidth(24)) ProgramMemory (
    .addr({ProgramCounterReg_pc_2, ProgramCounterReg_pc}), .data(ProgramMemory_data));
  Clock sysclk ();  // open: out
  Hex_Digit_Display hex_digit_display_2 (.value(ProgramCounterReg_pc[3:0]));  // open: dp
  Hex_Digit_Display hex_digit_display_3 (.value(ProgramCounterReg_pc[7:4]));  // open: dp
  Bloque1_bsr bloque1_bsr_1 (
    .opcode(BBUS[23:16]), .displacement(BBUS[15:5]), .Preload(bloque1_bsr_1_preload),
    .next_address(bloque1_bsr_1_next_address), .PC({ProgramCounterReg_pc_2, ProgramCounterReg_pc}), .CLK(CLK));
  // Probe on HOLD
  // Probe on UC1_HOLD
  // Probe on CLK
  // Probe on undriven
  // Probe on undriven_2
  // Probe on undriven_3
  // Probe on undriven_4[1]
  // Probe on undriven_4[0]
  // Probe on undriven_5
  ClockGenerator clocks (.Auto(1'b1), .ManualCLK(in_1), .CLK(CLK), .CLK2(CLK2), .CLK3(CLK3), .CLK4(CLK4));
  // Probe on ProgramMemory_data
  Bloque1_jmp bloque1_jmp_1 (
    .Preload(bloque1_jmp_1_preload), .register_to_test(register_bank_1_register_out_a_data), .CY(CYin),
    .opcode(BBUS[23:16]), .nxt_address(BBUS[15:5]), .next_address(bloque1_bsr_1_next_address));
  or or_1 (or_1_out, HOLD, UC1_HOLD);
  // Probe on bloque1_bsr_1_next_address
  or or_2 (or_2_out, bloque1_jmp_1_preload, bloque1_bsr_1_preload);
  Register #(.width(24)) InstructionRegister (.D(ProgramMemory_data), .clk(CLK), .Q(BBUS));  // open: en, clr
  PCreg ProgramCounterReg (
    .PC({ProgramCounterReg_pc_2, ProgramCounterReg_pc}),
    .displacement_or_address(bloque1_bsr_1_next_address), .HOLD(or_1_out), .CLK1(CLK), .Preload(or_2_out));
  // Probe on BBUS
  Hex_Digit_Display hex_digit_display_4 (.value(register_bank_viewer_1_c_data_msn));  // open: dp
  Hex_Digit_Display hex_digit_display_5 (.value(register_bank_viewer_1_c_data_lsn));  // open: dp
  DipSwitch #(.number(16)) dipswitch_1 (
    .sw1(dipswitch_1_sw16[15]), .sw2(dipswitch_1_sw16[14]), .sw3(dipswitch_1_sw16[13]),
    .sw4(dipswitch_1_sw16[12]), .sw5(dipswitch_1_sw16[11]), .sw6(dipswitch_1_sw16[10]),
    .sw7(dipswitch_1_sw16[9]), .sw8(dipswitch_1_sw16[8]), .sw9(dipswitch_1_sw16[7]),
    .sw10(dipswitch_1_sw16[6]), .sw11(dipswitch_1_sw16[5]), .sw12(dipswitch_1_sw16[4]),
    .sw13(dipswitch_1_sw16[3]), .sw14(dipswitch_1_sw16[2]), .sw15(dipswitch_1_sw16[1]),
    .sw16(dipswitch_1_sw16[0]));
  or or_3 (or_3_out, HOLD, UC1_HOLD);
  LED led_1 (.in(register_bank_viewer_1_c_is_enabled));
  Hex_Digit_Display hex_digit_display_6 (.value(register_bank_viewer_1_c_address_n3));  // open: dp
  Hex_Digit_Display hex_digit_display_7 (.value(register_bank_viewer_1_c_address_n2));  // open: dp
  DotMatrix #(.matrixcols(32), .matrixrows(32)) dotmatrix_1 (
    .col0(output_ports_viewer_1_mat_0_col_3_2), .col1(output_ports_viewer_1_mat_0_col_3_4),
    .col2(output_ports_viewer_1_mat_0_col_3_6), .col3(output_ports_viewer_1_mat_0_col_3_8),
    .col4(output_ports_viewer_1_mat_0_col_3), .col5(output_ports_viewer_1_mat_0_col_3_3),
    .col6(output_ports_viewer_1_mat_0_col_3_5), .col7(output_ports_viewer_1_mat_0_col_3_7),
    .col8(output_ports_viewer_1_mat_0_col_2), .col9(output_ports_viewer_1_mat_0_col_2_3),
    .col10(output_ports_viewer_1_mat_0_col_2_5), .col11(output_ports_viewer_1_mat_0_col_2_7),
    .col12(output_ports_viewer_1_mat_0_col_2_2), .col13(output_ports_viewer_1_mat_0_col_2_4),
    .col14(output_ports_viewer_1_mat_0_col_2_6), .col15(output_ports_viewer_1_mat_0_col_2_8),
    .col16(output_ports_viewer_1_mat_0_col_1), .col17(output_ports_viewer_1_mat_0_col_1_3),
    .col18(output_ports_viewer_1_mat_0_col_1_5), .col19(output_ports_viewer_1_mat_0_col_1_7),
    .col20(output_ports_viewer_1_mat_0_col_1_2), .col21(output_ports_viewer_1_mat_0_col_1_4),
    .col22(output_ports_viewer_1_mat_0_col_1_6), .col23(output_ports_viewer_1_mat_0_col_1_8),
    .col24(output_ports_viewer_1_mat_0_col_0_2), .col25(output_ports_viewer_1_mat_0_col_0_4),
    .col26(output_ports_viewer_1_mat_0_col_0_6), .col27(output_ports_viewer_1_mat_0_col_0_8),
    .col28(output_ports_viewer_1_mat_0_col_0), .col29(output_ports_viewer_1_mat_0_col_0_3),
    .col30(output_ports_viewer_1_mat_0_col_0_5), .col31(output_ports_viewer_1_mat_0_col_0_7));
  clk_edge_viewer clk_edge_viewer_1 (
    .out_7(clk_edge_viewer_1_out_7), .out_5(clk_edge_viewer_1_out_5), .out_3(clk_edge_viewer_1_out_3),
    .in_1(CLK2), .out_6(clk_edge_viewer_1_out_6), .out_9(clk_edge_viewer_1_out_9),
    .out_8(clk_edge_viewer_1_out_8), .out_2(clk_edge_viewer_1_out_2), .out_4(clk_edge_viewer_1_out_4));
  UC2_viewer uc2_viewer_1 (
    .out_7(uc2_viewer_1_out_7), .out_3(uc2_viewer_1_out_3), .out_6(uc2_viewer_1_out_6),
    .out_8(uc2_viewer_1_out_8), .out_4(uc2_viewer_1_out_4), .out_2(uc2_viewer_1_out_2),
    .out_9(uc2_viewer_1_out_9), .hold(UC1_HOLD), .out_5(uc2_viewer_1_out_5));
  DotMatrix #(.matrixcols(8), .matrixrows(8)) dotmatrix_2 (
    .col0(uc2_viewer_1_out_2), .col1(uc2_viewer_1_out_3), .col2(uc2_viewer_1_out_4),
    .col3(uc2_viewer_1_out_5), .col4(uc2_viewer_1_out_6), .col5(uc2_viewer_1_out_7),
    .col6(uc2_viewer_1_out_8), .col7(uc2_viewer_1_out_9));
  Hex_Digit_Display hex_digit_display_8 (.value(register_bank_viewer_1_c_address_n1));  // open: dp
  Hex_Digit_Display hex_digit_display_9 (.value(register_bank_viewer_1_c_address_n0));  // open: dp
  DipSwitch #(.number(16)) dipswitch_2 (
    .sw1(dipswitch_2_sw16[15]), .sw2(dipswitch_2_sw16[14]), .sw3(dipswitch_2_sw16[13]),
    .sw4(dipswitch_2_sw16[12]), .sw5(dipswitch_2_sw16[11]), .sw6(dipswitch_2_sw16[10]),
    .sw7(dipswitch_2_sw16[9]), .sw8(dipswitch_2_sw16[8]), .sw9(dipswitch_2_sw16[7]),
    .sw10(dipswitch_2_sw16[6]), .sw11(dipswitch_2_sw16[5]), .sw12(dipswitch_2_sw16[4]),
    .sw13(dipswitch_2_sw16[3]), .sw14(dipswitch_2_sw16[2]), .sw15(dipswitch_2_sw16[1]),
    .sw16(dipswitch_2_sw16[0]));
  DotMatrix #(.matrixcols(8), .matrixrows(8)) dotmatrix_3 (
    .col0(clk_edge_viewer_1_out_2), .col1(clk_edge_viewer_1_out_3), .col2(clk_edge_viewer_1_out_4),
    .col3(clk_edge_viewer_1_out_5), .col4(clk_edge_viewer_1_out_6), .col5(clk_edge_viewer_1_out_7),
    .col6(clk_edge_viewer_1_out_8), .col7(clk_edge_viewer_1_out_9));
  Hex_Digit_Display hex_digit_display_10 (.value(register_bank_viewer_1_a_data_msn));  // open: dp
  Hex_Digit_Display hex_digit_display_11 (.value(output_ports_viewer_1_hex_disp_0_3));  // open: dp
  output_ports_viewer output_ports_viewer_1 (
    .hex_disp_1_0(output_ports_viewer_1_hex_disp_1_0), .MAT_0_COL_0_7(output_ports_viewer_1_mat_0_col_0_7),
    .MAT_0_COL_1_7(output_ports_viewer_1_mat_0_col_1_7), .MAT_0_COL_2_7(output_ports_viewer_1_mat_0_col_2_7),
    .MAT_0_COL_3_7(output_ports_viewer_1_mat_0_col_3_7), .hex_disp_0_0(output_ports_viewer_1_hex_disp_0_0),
    .PO1(undriven_6), .PO0(undriven_7), .hex_disp_0_1(output_ports_viewer_1_hex_disp_0_1),
    .MAT_0_COL_3_5(output_ports_viewer_1_mat_0_col_3_5), .MAT_0_COL_2_5(output_ports_viewer_1_mat_0_col_2_5),
    .MAT_0_COL_1_5(output_ports_viewer_1_mat_0_col_1_5), .MAT_0_COL_0_5(output_ports_viewer_1_mat_0_col_0_5),
    .hex_disp_1_1(output_ports_viewer_1_hex_disp_1_1), .MAT_1_COL_3_5(output_ports_viewer_1_mat_1_col_3_5),
    .MAT_1_COL_3(output_ports_viewer_1_mat_1_col_3), .hex_disp_1_3(output_ports_viewer_1_hex_disp_1_3),
    .MAT_0_COL_0(output_ports_viewer_1_mat_0_col_0), .MAT_0_COL_1(output_ports_viewer_1_mat_0_col_1),
    .MAT_0_COL_2(output_ports_viewer_1_mat_0_col_2), .MAT_0_COL_3(output_ports_viewer_1_mat_0_col_3),
    .hex_disp_0_3(output_ports_viewer_1_hex_disp_0_3), .MAT_1_COL_3_7(output_ports_viewer_1_mat_1_col_3_7),
    .hex_disp_0_2(output_ports_viewer_1_hex_disp_0_2), .MAT_0_COL_3_3(output_ports_viewer_1_mat_0_col_3_3),
    .MAT_0_COL_2_3(output_ports_viewer_1_mat_0_col_2_3), .MAT_0_COL_1_3(output_ports_viewer_1_mat_0_col_1_3),
    .MAT_0_COL_0_3(output_ports_viewer_1_mat_0_col_0_3), .hex_disp_1_2(output_ports_viewer_1_hex_disp_1_2),
    .MAT_1_COL_3_3(output_ports_viewer_1_mat_1_col_3_3), .MAT_1_COL_2(output_ports_viewer_1_mat_1_col_2),
    .MAT_1_COL_2_3(output_ports_viewer_1_mat_1_col_2_3), .MAT_1_COL_2_5(output_ports_viewer_1_mat_1_col_2_5),
    .MAT_1_COL_2_7(output_ports_viewer_1_mat_1_col_2_7), .MAT_1_COL_1(output_ports_viewer_1_mat_1_col_1),
    .MAT_1_COL_1_3(output_ports_viewer_1_mat_1_col_1_3), .MAT_1_COL_1_5(output_ports_viewer_1_mat_1_col_1_5),
    .MAT_1_COL_1_7(output_ports_viewer_1_mat_1_col_1_7), .MAT_1_COL_0(output_ports_viewer_1_mat_1_col_0),
    .MAT_1_COL_0_3(output_ports_viewer_1_mat_1_col_0_3), .MAT_1_COL_0_5(output_ports_viewer_1_mat_1_col_0_5),
    .MAT_1_COL_0_7(output_ports_viewer_1_mat_1_col_0_7), .MAT_0_COL_3_2(output_ports_viewer_1_mat_0_col_3_2),
    .MAT_0_COL_3_4(output_ports_viewer_1_mat_0_col_3_4), .MAT_0_COL_3_6(output_ports_viewer_1_mat_0_col_3_6),
    .MAT_0_COL_3_8(output_ports_viewer_1_mat_0_col_3_8), .MAT_0_COL_2_2(output_ports_viewer_1_mat_0_col_2_2),
    .MAT_0_COL_2_4(output_ports_viewer_1_mat_0_col_2_4), .MAT_0_COL_2_6(output_ports_viewer_1_mat_0_col_2_6),
    .MAT_0_COL_2_8(output_ports_viewer_1_mat_0_col_2_8), .MAT_0_COL_1_2(output_ports_viewer_1_mat_0_col_1_2),
    .MAT_0_COL_1_4(output_ports_viewer_1_mat_0_col_1_4), .MAT_0_COL_1_6(output_ports_viewer_1_mat_0_col_1_6),
    .MAT_0_COL_1_8(output_ports_viewer_1_mat_0_col_1_8), .MAT_0_COL_0_2(output_ports_viewer_1_mat_0_col_0_2),
    .MAT_0_COL_0_4(output_ports_viewer_1_mat_0_col_0_4), .MAT_0_COL_0_6(output_ports_viewer_1_mat_0_col_0_6),
    .MAT_0_COL_0_8(output_ports_viewer_1_mat_0_col_0_8), .MAT_1_COL_3_2(output_ports_viewer_1_mat_1_col_3_2),
    .MAT_1_COL_3_4(output_ports_viewer_1_mat_1_col_3_4), .MAT_1_COL_3_6(output_ports_viewer_1_mat_1_col_3_6),
    .MAT_1_COL_3_8(output_ports_viewer_1_mat_1_col_3_8), .MAT_1_COL_2_2(output_ports_viewer_1_mat_1_col_2_2),
    .MAT_1_COL_2_4(output_ports_viewer_1_mat_1_col_2_4), .MAT_1_COL_2_6(output_ports_viewer_1_mat_1_col_2_6),
    .MAT_1_COL_2_8(output_ports_viewer_1_mat_1_col_2_8), .MAT_1_COL_1_2(output_ports_viewer_1_mat_1_col_1_2),
    .MAT_1_COL_1_4(output_ports_viewer_1_mat_1_col_1_4), .MAT_1_COL_1_6(output_ports_viewer_1_mat_1_col_1_6),
    .MAT_1_COL_1_8(output_ports_viewer_1_mat_1_col_1_8), .MAT_1_COL_0_2(output_ports_viewer_1_mat_1_col_0_2),
    .MAT_1_COL_0_4(output_ports_viewer_1_mat_1_col_0_4), .MAT_1_COL_0_6(output_ports_viewer_1_mat_1_col_0_6),
    .MAT_1_COL_0_8(output_ports_viewer_1_mat_1_col_0_8));
  // instruction2register instruction2register_1: pin names not known; wires that end beside it: BBUS, instruction2register_1_p2, instruction2register_1_p3, instruction2register_1_p4, instruction2register_1_p5, instruction2register_1_p6
  Hex_Digit_Display hex_digit_display_12 (.value(register_bank_viewer_1_a_data_lsn));  // open: dp
  Hex_Digit_Display hex_digit_display_13 (.value(register_bank_viewer_1_a_address_n3));  // open: dp
  Hex_Digit_Display hex_digit_display_14 (.value(output_ports_viewer_1_hex_disp_0_2));  // open: dp
  Hex_Digit_Display hex_digit_display_15 (.value(output_ports_viewer_1_hex_disp_0_1));  // open: dp
  Micro_Instruction_ROM MicroInstructionROM (
    .Instruction(BBUS), .MicroInstruction(MicroInstructionROM_microinstruction));
  LED led_2 (.in(register_bank_viewer_1_a_is_enabled));
  register_bank_viewer register_bank_viewer_1 (
    .A_is_enabled(register_bank_viewer_1_a_is_enabled), .B_address_N3(register_bank_viewer_1_b_address_n3),
    .A_address_N0(register_bank_viewer_1_a_address_n0), .C_is_enabled(register_bank_viewer_1_c_is_enabled),
    .B_data_MSN(register_bank_viewer_1_b_data_msn), .C_address_N0(register_bank_viewer_1_c_address_n0),
    .C_data_out(C_Etapa3), .C_data_MSN(register_bank_viewer_1_c_data_msn),
    .C_address_N2(register_bank_viewer_1_c_address_n2), .B_address_N1(register_bank_viewer_1_b_address_n1),
    .B_address_N2(register_bank_viewer_1_b_address_n2), .B_address(register_bank_1_register_out_b_data),
    .A_data_MSN(register_bank_viewer_1_a_data_msn), .A_address_N2(register_bank_viewer_1_a_address_n2),
    .A_address_N1(register_bank_viewer_1_a_address_n1), .A_data_out(A_Etapa1), .B_data_out(B_Etapa1),
    .C_data_LSN(register_bank_viewer_1_c_data_lsn), .C_address_N1(register_bank_viewer_1_c_address_n1),
    .C_address_N3(register_bank_viewer_1_c_address_n3), .A_data_LSN(register_bank_viewer_1_a_data_lsn),
    .A_address(register_bank_1_register_out_a_data), .C_address(reg_C_write),
    .B_address_N0(register_bank_viewer_1_b_address_n0), .B_data_LSN(register_bank_viewer_1_b_data_lsn),
    .A_address_N3(register_bank_viewer_1_a_address_n3), .B_is_enabled(register_bank_viewer_1_b_is_enabled));
  Hex_Digit_Display hex_digit_display_16 (.value(register_bank_viewer_1_a_address_n1));  // open: dp
  Hex_Digit_Display hex_digit_display_17 (.value(register_bank_viewer_1_a_address_n2));  // open: dp
  DotMatrix #(.matrixcols(32), .matrixrows(32)) dotmatrix_4 (
    .col0(output_ports_viewer_1_mat_1_col_3), .col1(output_ports_viewer_1_mat_1_col_3_3),
    .col2(output_ports_viewer_1_mat_1_col_3_5), .col3(output_ports_viewer_1_mat_1_col_3_7),
    .col4(output_ports_viewer_1_mat_1_col_3_2), .col5(output_ports_viewer_1_mat_1_col_3_4),
    .col6(output_ports_viewer_1_mat_1_col_3_6), .col7(output_ports_viewer_1_mat_1_col_3_8),
    .col8(output_ports_viewer_1_mat_1_col_2), .col9(output_ports_viewer_1_mat_1_col_2_3),
    .col10(output_ports_viewer_1_mat_1_col_2_5), .col11(output_ports_viewer_1_mat_1_col_2_7),
    .col12(output_ports_viewer_1_mat_1_col_2_2), .col13(output_ports_viewer_1_mat_1_col_2_4),
    .col14(output_ports_viewer_1_mat_1_col_2_6), .col15(output_ports_viewer_1_mat_1_col_2_8),
    .col16(output_ports_viewer_1_mat_1_col_1), .col17(output_ports_viewer_1_mat_1_col_1_3),
    .col18(output_ports_viewer_1_mat_1_col_1_5), .col19(output_ports_viewer_1_mat_1_col_1_7),
    .col20(output_ports_viewer_1_mat_1_col_1_2), .col21(output_ports_viewer_1_mat_1_col_1_4),
    .col22(output_ports_viewer_1_mat_1_col_1_6), .col23(output_ports_viewer_1_mat_1_col_1_8),
    .col24(output_ports_viewer_1_mat_1_col_0), .col25(output_ports_viewer_1_mat_1_col_0_3),
    .col26(output_ports_viewer_1_mat_1_col_0_5), .col27(output_ports_viewer_1_mat_1_col_0_7),
    .col28(output_ports_viewer_1_mat_1_col_0_2), .col29(output_ports_viewer_1_mat_1_col_0_4),
    .col30(output_ports_viewer_1_mat_1_col_0_6), .col31(output_ports_viewer_1_mat_1_col_0_8));
  Hex_Digit_Display hex_digit_display_18 (.value(output_ports_viewer_1_hex_disp_0_0));  // open: dp
  DotMatrix #(.matrixcols(17), .matrixrows(4)) dotmatrix_5 (
    .col0(pipeline_register_viewer_1_b16), .col1(pipeline_register_viewer_1_b15),
    .col2(pipeline_register_viewer_1_b14), .col3(pipeline_register_viewer_1_b13),
    .col4(pipeline_register_viewer_1_b12), .col5(pipeline_register_viewer_1_b11),
    .col6(pipeline_register_viewer_1_b10), .col7(pipeline_register_viewer_1_b9),
    .col8(pipeline_register_viewer_1_b8), .col9(pipeline_register_viewer_1_b7),
    .col10(pipeline_register_viewer_1_b6), .col11(pipeline_register_viewer_1_b5),
    .col12(pipeline_register_viewer_1_b4), .col13(pipeline_register_viewer_1_b3),
    .col14(pipeline_register_viewer_1_b2), .col15(pipeline_register_viewer_1_b1),
    .col16(pipeline_register_viewer_1_b0));
  pipeline_register_viewer pipeline_register_viewer_1 (
    .A_in(A_Etapa1), .b15(pipeline_register_viewer_1_b15), .b2(pipeline_register_viewer_1_b2),
    .A_MSN(pipeline_register_viewer_1_a_msn), .b11(pipeline_register_viewer_1_b11),
    .b14(pipeline_register_viewer_1_b14), .B_is_enabled(pipeline_register_viewer_1_b_is_enabled),
    .b7(pipeline_register_viewer_1_b7), .b10(pipeline_register_viewer_1_b10),
    .microinstruction({pipeline_register_1_aluc_out, pipeline_register_1_sh_out, pipeline_register_1_kmx_out[8], pipeline_register_1_mrymw_out, pipeline_register_1_t_bus_out}),
    .b3(pipeline_register_viewer_1_b3), .b6(pipeline_register_viewer_1_b6),
    .b16(pipeline_register_viewer_1_b16), .b1(pipeline_register_viewer_1_b1), .B_in(B_Etapa1),
    .b12(pipeline_register_viewer_1_b12), .b5(pipeline_register_viewer_1_b5),
    .B_MSN(pipeline_register_viewer_1_b_msn), .b8(pipeline_register_viewer_1_b8),
    .b9(pipeline_register_viewer_1_b9), .A_LSN(pipeline_register_viewer_1_a_lsn),
    .b4(pipeline_register_viewer_1_b4), .b13(pipeline_register_viewer_1_b13),
    .A_is_enabled(pipeline_register_viewer_1_a_is_enabled), .b0(pipeline_register_viewer_1_b0),
    .C_in(C_Etapa1), .B_LSN(pipeline_register_viewer_1_b_lsn),
    .C_is_enabled(pipeline_register_viewer_1_c_is_enabled), .C_MSN(pipeline_register_viewer_1_c_msn),
    .C_LSN(pipeline_register_viewer_1_c_lsn));
  // Probe on MicroInstructionROM_microinstruction[14:11]
  // Probe on MicroInstructionROM_microinstruction[10:9]
  // Probe on MicroInstructionROM_microinstruction[8]
  // Probe on MicroInstructionROM_microinstruction[7]
  // Probe on MicroInstructionROM_microinstruction[6]
  // Probe on MicroInstructionROM_microinstruction[5:0]
  Hex_Digit_Display hex_digit_display_19 (.value(register_bank_viewer_1_a_address_n0));  // open: dp
  Hex_Digit_Display hex_digit_display_20 (.value(output_ports_viewer_1_hex_disp_1_3));  // open: dp
  Hex_Digit_Display hex_digit_display_21 (.value(register_bank_viewer_1_b_data_msn));  // open: dp
  Hex_Digit_Display hex_digit_display_22 (.value(output_ports_viewer_1_hex_disp_1_2));  // open: dp
  Hex_Digit_Display hex_digit_display_23 (.value(output_ports_viewer_1_hex_disp_1_1));  // open: dp
  Hex_Digit_Display hex_digit_display_24 (.value(register_bank_viewer_1_b_data_lsn));  // open: dp
  Hex_Digit_Display hex_digit_display_25 (.value(register_bank_viewer_1_b_address_n3));  // open: dp
  Hex_Digit_Display hex_digit_display_26 (.value(output_ports_viewer_1_hex_disp_1_0));  // open: dp
  Hex_Digit_Display hex_digit_display_27 (.value(pipeline_register_viewer_1_c_msn));  // open: dp
  not not_1 (not_1_out, MEM_is_done);
  LED led_3 (.in(register_bank_viewer_1_b_is_enabled));
  Hex_Digit_Display hex_digit_display_28 (.value(register_bank_viewer_1_b_address_n2));  // open: dp
  Hex_Digit_Display hex_digit_display_29 (.value(register_bank_viewer_1_b_address_n1));  // open: dp
  LED led_4 (.in(pipeline_register_viewer_1_c_is_enabled));
  Hex_Digit_Display hex_digit_display_30 (.value(pipeline_register_viewer_1_c_lsn));  // open: dp
  // Probe on pipeline_register_1_aluc_out
  Pipeline_register pipeline_register_1 (
    .ALUC_OUT(pipeline_register_1_aluc_out), .B_bus_IN(instruction2register_1_p4),
    .SH_IN(MicroInstructionROM_microinstruction[10:9]), .D_Address_OUT(pipeline_register_1_d_address_out),
    .C_bus_OUT(C_Etapa1), .A_bus_OUT(A_Etapa1), .ALUC_IN(MicroInstructionROM_microinstruction[14:11]),
    .A_bus_IN(instruction2register_1_p3), .D_Address_IN(instruction2register_1_p2),
    .MRyMW_OUT(pipeline_register_1_mrymw_out), .SH_OUT(pipeline_register_1_sh_out),
    .C_bus_IN(instruction2register_1_p5), .Kmx_IN(MicroInstructionROM_microinstruction[8]), .Hold(or_3_out),
    .B_bus_OUT(B_Etapa1), .T_bus_OUT(pipeline_register_1_t_bus_out), .CLK(CLK2),
    .MRyMW_IN(MicroInstructionROM_microinstruction[7:6]),
    .T_bus_IN(MicroInstructionROM_microinstruction[5:0]), .Kmx_OUT(pipeline_register_1_kmx_out[8]));
  Hex_Digit_Display hex_digit_display_31 (.value(register_bank_viewer_1_b_address_n0));  // open: dp
  LED led_5 (.in(pipeline_register_viewer_1_a_is_enabled));
  Hex_Digit_Display hex_digit_display_32 (.value(pipeline_register_viewer_1_a_lsn));  // open: dp
  Hex_Digit_Display hex_digit_display_33 (.value(pipeline_register_viewer_1_a_msn));  // open: dp
  // Probe on A_Etapa1
  // Probe on B_Etapa1
  // Probe on C_Etapa1
  register_bank register_bank_1 (
    .clk(CLK), .register_out_B_data(register_bank_1_register_out_b_data), .register_out_A_address(A_Etapa1),
    .register_out_B_address(B_Etapa1), .register_out_A_data(register_bank_1_register_out_a_data),
    .register_in_data(reg_C_write), .register_in_address(C_Etapa3));  // open: register_out_aux_address, register_out_aux_data
  LED led_6 (.in(pipeline_register_viewer_1_b_is_enabled));
  Hex_Digit_Display hex_digit_display_34 (.value(pipeline_register_viewer_1_b_lsn));  // open: dp
  Hex_Digit_Display hex_digit_display_35 (.value(pipeline_register_viewer_1_b_msn));  // open: dp
  // Probe on C_Etapa3
  // UC1 uc1_1: pin names not known; wires that end beside it: HOLD, pipeline_register_1_mrymw_out, not_1_out, mem_is_free, uc1_1_p5, uc1_1_p6, LatchMemEnable, UC1_HOLD
  Register #(.width(1)) register_1 (.D(uc1_1_p5), .clk(CLK2), .Q(register_1_q));  // open: en, clr
  Register #(.width(16), .trigger("falling")) Constant_K (
    .D(instruction2register_1_p6), .clk(CLK2), .Q(Constant_K_q));  // open: en, clr
  Register #(.width(1), .trigger("falling")) register_2 (.D(uc1_1_p6), .clk(CLK2), .Q(register_2_q));  // open: en, clr
  not not_2 (not_2_out, pipeline_register_1_kmx_out[8]);
  Register #(.width(16)) BusA_ALU (.D(multiplexer_1_out), .en(uc1_1_p5), .clk(CLK2), .Q(BusA_ALU_q));  // open: clr
  Multiplexer #(.width(16), .enable("false")) multiplexer_1 (
    .in0(Constant_K_q), .in1(register_bank_1_register_out_a_data), .out(multiplexer_1_out), .sel(not_2_out));
  Register #(.width(16)) BusB_ALU (
    .D(register_bank_1_register_out_b_data), .en(uc1_1_p5), .clk(CLK2), .Q(BusB_ALU_q));  // open: clr
  Register #(.width(10), .trigger("falling")) register_3 (
    .D(pipeline_register_1_d_address_out), .en(uc1_1_p6), .clk(CLK2), .Q(register_3_q));  // open: clr
  DotMatrix #(.matrixcols(17), .matrixrows(4)) dotmatrix_6 (
    .col0(pipeline_register_viewer_2_b16), .col1(pipeline_register_viewer_2_b15),
    .col2(pipeline_register_viewer_2_b14), .col3(pipeline_register_viewer_2_b13),
    .col4(pipeline_register_viewer_2_b12), .col5(pipeline_register_viewer_2_b11),
    .col6(pipeline_register_viewer_2_b10), .col7(pipeline_register_viewer_2_b9),
    .col8(pipeline_register_viewer_2_b8), .col9(pipeline_register_viewer_2_b7),
    .col10(pipeline_register_viewer_2_b6), .col11(pipeline_register_viewer_2_b5),
    .col12(pipeline_register_viewer_2_b4), .col13(pipeline_register_viewer_2_b3),
    .col14(pipeline_register_viewer_2_b2), .col15(pipeline_register_viewer_2_b1),
    .col16(pipeline_register_viewer_2_b0));
  pipeline_register_viewer pipeline_register_viewer_2 (
    .A_in(ALU_Pipeline_a_bus_out), .b15(pipeline_register_viewer_2_b15), .b2(pipeline_register_viewer_2_b2),
    .A_MSN(pipeline_register_viewer_2_a_msn), .b11(pipeline_register_viewer_2_b11),
    .b14(pipeline_register_viewer_2_b14), .B_is_enabled(pipeline_register_viewer_2_b_is_enabled),
    .b7(pipeline_register_viewer_2_b7), .b10(pipeline_register_viewer_2_b10),
    .microinstruction({ALU_Pipeline_aluc_out, ALU_Pipeline_sh_out, ALU_Pipeline_kmx_out[8], MREtapa2Pipeline, ALU_Pipeline_t_bus_out}),
    .b3(pipeline_register_viewer_2_b3), .b6(pipeline_register_viewer_2_b6),
    .b16(pipeline_register_viewer_2_b16), .b1(pipeline_register_viewer_2_b1), .B_in(ALU_Pipeline_b_bus_out),
    .b12(pipeline_register_viewer_2_b12), .b5(pipeline_register_viewer_2_b5),
    .B_MSN(pipeline_register_viewer_2_b_msn), .b8(pipeline_register_viewer_2_b8),
    .b9(pipeline_register_viewer_2_b9), .A_LSN(pipeline_register_viewer_2_a_lsn),
    .b4(pipeline_register_viewer_2_b4), .b13(pipeline_register_viewer_2_b13),
    .A_is_enabled(pipeline_register_viewer_2_a_is_enabled), .b0(pipeline_register_viewer_2_b0),
    .C_in(C_Etapa2Alu), .B_LSN(pipeline_register_viewer_2_b_lsn),
    .C_is_enabled(pipeline_register_viewer_2_c_is_enabled), .C_MSN(pipeline_register_viewer_2_c_msn),
    .C_LSN(pipeline_register_viewer_2_c_lsn));
  not not_3 (not_3_out, uc1_1_p5);
  and and_1 (and_1_out, ~CLK3, register_2_q);  // AND_Gate
  Register #(.width(16), .trigger("falling")) BusA_LS (
    .D(register_bank_1_register_out_a_data), .en(uc1_1_p6), .clk(CLK2), .Q(BusA_LS_q));  // open: clr
  // Probe on BusA_ALU_q
  // Probe on BusB_ALU_q
  DotMatrix #(.matrixcols(17), .matrixrows(4)) dotmatrix_7 (
    .col0(pipeline_register_viewer_3_b16), .col1(pipeline_register_viewer_3_b15),
    .col2(pipeline_register_viewer_3_b14), .col3(pipeline_register_viewer_3_b13),
    .col4(pipeline_register_viewer_3_b12), .col5(pipeline_register_viewer_3_b11),
    .col6(pipeline_register_viewer_3_b10), .col7(pipeline_register_viewer_3_b9),
    .col8(pipeline_register_viewer_3_b8), .col9(pipeline_register_viewer_3_b7),
    .col10(pipeline_register_viewer_3_b6), .col11(pipeline_register_viewer_3_b5),
    .col12(pipeline_register_viewer_3_b4), .col13(pipeline_register_viewer_3_b3),
    .col14(pipeline_register_viewer_3_b2), .col15(pipeline_register_viewer_3_b1),
    .col16(pipeline_register_viewer_3_b0));
  pipeline_register_viewer pipeline_register_viewer_3 (
    .A_in(LoadStore_a_bus_out), .b15(pipeline_register_viewer_3_b15), .b2(pipeline_register_viewer_3_b2),
    .A_MSN(pipeline_register_viewer_3_a_msn), .b11(pipeline_register_viewer_3_b11),
    .b14(pipeline_register_viewer_3_b14), .B_is_enabled(pipeline_register_viewer_3_b_is_enabled),
    .b7(pipeline_register_viewer_3_b7), .b10(pipeline_register_viewer_3_b10),
    .microinstruction({LoadStore_t_bus_out[14:8], MRMW, LoadStore_t_bus_out[5:0]}),
    .b3(pipeline_register_viewer_3_b3), .b6(pipeline_register_viewer_3_b6),
    .b16(pipeline_register_viewer_3_b16), .b1(pipeline_register_viewer_3_b1), .B_in(LoadStore_b_bus_out),
    .b12(pipeline_register_viewer_3_b12), .b5(pipeline_register_viewer_3_b5),
    .B_MSN(pipeline_register_viewer_3_b_msn), .b8(pipeline_register_viewer_3_b8),
    .b9(pipeline_register_viewer_3_b9), .A_LSN(pipeline_register_viewer_3_a_lsn),
    .b4(pipeline_register_viewer_3_b4), .b13(pipeline_register_viewer_3_b13),
    .A_is_enabled(pipeline_register_viewer_3_a_is_enabled), .b0(pipeline_register_viewer_3_b0),
    .C_in(C_Etapa2Mem), .B_LSN(pipeline_register_viewer_3_b_lsn),
    .C_is_enabled(pipeline_register_viewer_3_c_is_enabled), .C_MSN(pipeline_register_viewer_3_c_msn),
    .C_LSN(pipeline_register_viewer_3_c_lsn));
  not not_4 (not_4_out, uc1_1_p6);
  Register #(.width(1)) register_4 (.D(ALUALULAU_cyout), .en(1'b1), .clk(CLK2), .Q(CYin));  // open: clr
  LED led_7 (.in(pipeline_register_viewer_2_c_is_enabled));
  Hex_Digit_Display hex_digit_display_36 (.value(pipeline_register_viewer_2_c_msn));  // open: dp
  or or_4 (or_4_out, mem_is_free, nor_1_out);
  nor nor_1 (nor_1_out, mem_is_free, MEM_is_done);
  and and_2 (and_2_out, register_1_q, CLK3);
  ALU ALUALULAU (
    .ALUC(ALU_Pipeline_aluc_out), .A(BusA_ALU_q), .B(BusB_ALU_q), .CYin(CYin), .Z(ALUALULAU_z),
    .CYout(ALUALULAU_cyout));
  LED led_8 (.in(pipeline_register_viewer_2_a_is_enabled));
  Hex_Digit_Display hex_digit_display_37 (.value(pipeline_register_viewer_2_c_lsn));  // open: dp
  Hex_Digit_Display hex_digit_display_38 (.value(pipeline_register_viewer_2_a_msn));  // open: dp
  Pipeline_register ALU_Pipeline (
    .ALUC_OUT(ALU_Pipeline_aluc_out), .B_bus_IN(B_Etapa1), .SH_IN(pipeline_register_1_sh_out),
    .D_Address_OUT(ALU_Pipeline_d_address_out), .C_bus_OUT(C_Etapa2Alu), .A_bus_OUT(ALU_Pipeline_a_bus_out),
    .ALUC_IN(pipeline_register_1_aluc_out), .A_bus_IN(A_Etapa1),
    .D_Address_IN(pipeline_register_1_d_address_out), .MRyMW_OUT(MREtapa2Pipeline),
    .SH_OUT(ALU_Pipeline_sh_out), .C_bus_IN(C_Etapa1), .Kmx_IN(pipeline_register_1_kmx_out[8]),
    .Hold(not_3_out), .B_bus_OUT(ALU_Pipeline_b_bus_out), .T_bus_OUT(ALU_Pipeline_t_bus_out), .CLK(CLK3),
    .MRyMW_IN(pipeline_register_1_mrymw_out), .T_bus_IN(pipeline_register_1_t_bus_out),
    .Kmx_OUT(ALU_Pipeline_kmx_out[8]));
  and and_3 (and_3_out, ~uc1_1_p5, or_4_out);  // AND_Gate
  // Probe on ALUALULAU_z
  LED led_9 (.in(pipeline_register_viewer_3_c_is_enabled));
  Hex_Digit_Display hex_digit_display_39 (.value(pipeline_register_viewer_3_c_lsn));  // open: dp
  Hex_Digit_Display hex_digit_display_40 (.value(pipeline_register_viewer_3_c_msn));  // open: dp
  Pipeline_register LoadStore (
    .ALUC_OUT(LoadStore_t_bus_out[14:11]), .B_bus_IN(B_Etapa1), .SH_IN(pipeline_register_1_sh_out),
    .D_Address_OUT(LoadStore_d_address_out), .C_bus_OUT(C_Etapa2Mem), .A_bus_OUT(LoadStore_a_bus_out),
    .ALUC_IN(pipeline_register_1_aluc_out), .A_bus_IN(A_Etapa1),
    .D_Address_IN(pipeline_register_1_d_address_out), .MRyMW_OUT(MRMW), .SH_OUT(LoadStore_t_bus_out[10:9]),
    .C_bus_IN(C_Etapa1), .Kmx_IN(pipeline_register_1_kmx_out[8]), .Hold(not_4_out),
    .B_bus_OUT(LoadStore_b_bus_out), .T_bus_OUT(LoadStore_t_bus_out[5:0]), .CLK(CLK3),
    .MRyMW_IN(pipeline_register_1_mrymw_out), .T_bus_IN(pipeline_register_1_t_bus_out),
    .Kmx_OUT(LoadStore_t_bus_out[8]));
  and and_4 (and_4_out, MEM_is_done, ~mem_is_free);  // AND_Gate
  Hex_Digit_Display hex_digit_display_41 (.value(pipeline_register_viewer_2_a_lsn));  // open: dp
  Hex_Digit_Display hex_digit_display_42 (.value(pipeline_register_viewer_2_b_msn));  // open: dp
  LED led_10 (.in(pipeline_register_viewer_3_a_is_enabled));
  Hex_Digit_Display hex_digit_display_43 (.value(pipeline_register_viewer_3_a_msn));  // open: dp
  Hex_Digit_Display hex_digit_display_44 (.value(pipeline_register_viewer_3_a_lsn));  // open: dp
  Data data_1 (
    .DAddress(register_3_q), .M(MRMW), .clk(CLK2), .Enable(register_2_q), .DataMemInput(BusA_LS_q),
    .DataMemOut(data_1_datamemout));
  LED led_11 (.in(pipeline_register_viewer_2_b_is_enabled));
  Hex_Digit_Display hex_digit_display_45 (.value(pipeline_register_viewer_2_b_lsn));  // open: dp
  Register #(.width(16)) register_5 (.D(shiftersh_1_out_3), .en(1'b1), .clk(CLK2), .Q(ALU_RESULT));  // open: clr
  // Probe on shiftersh_1_out_3
  ShifterSH shiftersh_1 (.ShifterIn(ALUALULAU_z), .SH(ALU_Pipeline_sh_out), .out_3(shiftersh_1_out_3));
  LED led_12 (.in(pipeline_register_viewer_3_b_is_enabled));
  Hex_Digit_Display hex_digit_display_46 (.value(pipeline_register_viewer_3_b_msn));  // open: dp
  // Probe on MRMW
  // Probe on LoadStore_d_address_out
  // Probe on data_1_datamemout
  ALU_unit_control alu_unit_control_1 (
    .set_free(and_3_out), .set_not_free(and_2_out), .clk(CLK3), .is_free(ALU_is_free), .is_done(ALU_is_done));
  Hex_Digit_Display hex_digit_display_47 (.value(pipeline_register_viewer_3_b_lsn));  // open: dp
  // Probe on mem_is_free
  memory_unit_control memory_unit_control_1 (
    .set_free(and_4_out), .set_not_free(and_1_out), .clk(CLK2), .is_free(mem_is_free), .is_done(MEM_is_done));
  Register #(.width(16)) register_6 (.D(data_1_datamemout), .en(1'b1), .clk(CLK2), .Q(register_6_q));  // open: clr
  DotMatrix #(.inputtype("row"), .matrixcols(16), .matrixrows(16)) dotmatrix_8 ();  // open: row0, row1, row2, row3, row4, row5, row6, row7, row8, row9, row10, row11, row12, row13, row14, row15
  // stage2_status_viewer stage2_status_viewer_1: pin names not known; wires that end beside it: ALU_is_free, ALU_is_done
  DotMatrix #(.inputtype("row"), .matrixcols(16), .matrixrows(16)) dotmatrix_9 ();  // open: row0, row1, row2, row3, row4, row5, row6, row7, row8, row9, row10, row11, row12, row13, row14, row15
  DotMatrix #(.inputtype("row"), .matrixcols(16), .matrixrows(16)) dotmatrix_10 ();  // open: row0, row1, row2, row3, row4, row5, row6, row7, row8, row9, row10, row11, row12, row13, row14, row15
  Multiplexer #(.width(16), .enable("false")) multiplexer_2 (
    .in0(ALU_RESULT), .in1(register_6_q), .out(reg_C_write), .sel(MEM_is_done));
  // stage2_status_viewer stage2_status_viewer_2: pin names not known; wires that end beside it: mem_is_free, MEM_is_done
  DotMatrix #(.inputtype("row"), .matrixcols(16), .matrixrows(16)) dotmatrix_11 ();  // open: row0, row1, row2, row3, row4, row5, row6, row7, row8, row9, row10, row11, row12, row13, row14, row15
  DotMatrix #(.inputtype("row"), .matrixcols(16), .matrixrows(16)) dotmatrix_12 ();  // open: row0, row1, row2, row3, row4, row5, row6, row7, row8, row9, row10, row11, row12, row13, row14, row15
  DotMatrix #(.inputtype("row"), .matrixcols(16), .matrixrows(16)) dotmatrix_13 ();  // open: row0, row1, row2, row3, row4, row5, row6, row7, row8, row9, row10, row11, row12, row13, row14, row15
  judge judge_1 (
    .reg_in_alu({ALU_Pipeline_aluc_out, ALU_Pipeline_sh_out, ALU_Pipeline_kmx_out[8], MREtapa2Pipeline, ALU_Pipeline_t_bus_out}),
    .reg_in_memory({LoadStore_t_bus_out[14:8], MRMW, LoadStore_t_bus_out[5:0]}),
    .A_alu(ALU_Pipeline_a_bus_out), .A_mem(LoadStore_a_bus_out), .B_alu(ALU_Pipeline_b_bus_out),
    .B_mem(LoadStore_b_bus_out), .C_alu(C_Etapa2Alu), .C_mem(C_Etapa2Mem), .in_9({MEM_is_done, ALU_is_done}),
    .reg_out(judge_1_reg_out), .A_bus(judge_1_a_bus), .B_bus(judge_1_b_bus), .C_bus(judge_1_c_bus));
  UC2 uc2_1 (
    .A_etapa_1(A_Etapa1), .B_etapa_1(B_Etapa1), .C_etapa_1(C_Etapa1), .C_etapa_2_ALU(C_Etapa2Alu),
    .ALU_is_done(ALU_is_free), .C_etapa_2_MEM(C_Etapa2Mem), .MEM_is_done(mem_is_free), .C_etapa_3(C_Etapa3),
    .clk(CLK), .out_10(HOLD));
  UC2_viewer uc2_viewer_2 (
    .out_7(uc2_viewer_2_out_7), .out_3(uc2_viewer_2_out_3), .out_6(uc2_viewer_2_out_6),
    .out_8(uc2_viewer_2_out_8), .out_4(uc2_viewer_2_out_4), .out_2(uc2_viewer_2_out_2),
    .out_9(uc2_viewer_2_out_9), .hold(HOLD), .out_5(uc2_viewer_2_out_5));
  DotMatrix #(.matrixcols(8), .matrixrows(8)) dotmatrix_14 (
    .col0(uc2_viewer_2_out_2), .col1(uc2_viewer_2_out_3), .col2(uc2_viewer_2_out_4),
    .col3(uc2_viewer_2_out_5), .col4(uc2_viewer_2_out_6), .col5(uc2_viewer_2_out_7),
    .col6(uc2_viewer_2_out_8), .col7(uc2_viewer_2_out_9));
  pipeline_register_viewer pipeline_register_viewer_4 (
    .A_in(pipeline_register_2_a_bus_out), .b15(pipeline_register_viewer_4_b15),
    .b2(pipeline_register_viewer_4_b2), .A_MSN(pipeline_register_viewer_4_a_msn),
    .b11(pipeline_register_viewer_4_b11), .b14(pipeline_register_viewer_4_b14),
    .B_is_enabled(pipeline_register_viewer_4_b_is_enabled), .b7(pipeline_register_viewer_4_b7),
    .b10(pipeline_register_viewer_4_b10), .microinstruction(pipeline_register_2_t_bus_out),
    .b3(pipeline_register_viewer_4_b3), .b6(pipeline_register_viewer_4_b6),
    .b16(pipeline_register_viewer_4_b16), .b1(pipeline_register_viewer_4_b1),
    .B_in(pipeline_register_2_b_bus_out), .b12(pipeline_register_viewer_4_b12),
    .b5(pipeline_register_viewer_4_b5), .B_MSN(pipeline_register_viewer_4_b_msn),
    .b8(pipeline_register_viewer_4_b8), .b9(pipeline_register_viewer_4_b9),
    .A_LSN(pipeline_register_viewer_4_a_lsn), .b4(pipeline_register_viewer_4_b4),
    .b13(pipeline_register_viewer_4_b13), .A_is_enabled(pipeline_register_viewer_4_a_is_enabled),
    .b0(pipeline_register_viewer_4_b0), .C_in(C_Etapa3), .B_LSN(pipeline_register_viewer_4_b_lsn),
    .C_is_enabled(pipeline_register_viewer_4_c_is_enabled), .C_MSN(pipeline_register_viewer_4_c_msn),
    .C_LSN(pipeline_register_viewer_4_c_lsn));
  DotMatrix #(.matrixcols(17), .matrixrows(4)) dotmatrix_15 (
    .col0(pipeline_register_viewer_4_b16), .col1(pipeline_register_viewer_4_b15),
    .col2(pipeline_register_viewer_4_b14), .col3(pipeline_register_viewer_4_b13),
    .col4(pipeline_register_viewer_4_b12), .col5(pipeline_register_viewer_4_b11),
    .col6(pipeline_register_viewer_4_b10), .col7(pipeline_register_viewer_4_b9),
    .col8(pipeline_register_viewer_4_b8), .col9(pipeline_register_viewer_4_b7),
    .col10(pipeline_register_viewer_4_b6), .col11(pipeline_register_viewer_4_b5),
    .col12(pipeline_register_viewer_4_b4), .col13(pipeline_register_viewer_4_b3),
    .col14(pipeline_register_viewer_4_b2), .col15(pipeline_register_viewer_4_b1),
    .col16(pipeline_register_viewer_4_b0));
  LED led_13 (.in(pipeline_register_viewer_4_c_is_enabled));
  Hex_Digit_Display hex_digit_display_48 (.value(pipeline_register_viewer_4_c_msn));  // open: dp
  Hex_Digit_Display hex_digit_display_49 (.value(pipeline_register_viewer_4_c_lsn));  // open: dp
  Pipeline_register pipeline_register_2 (
    .ALUC_OUT(pipeline_register_2_t_bus_out[14:11]), .B_bus_IN(judge_1_b_bus), .SH_IN(judge_1_reg_out[10:9]),
    .C_bus_OUT(C_Etapa3), .A_bus_OUT(pipeline_register_2_a_bus_out), .ALUC_IN(judge_1_reg_out[14:11]),
    .A_bus_IN(judge_1_a_bus), .MRyMW_OUT(pipeline_register_2_t_bus_out[7:6]),
    .SH_OUT(pipeline_register_2_t_bus_out[10:9]), .C_bus_IN(judge_1_c_bus), .Kmx_IN(judge_1_reg_out[8]),
    .Hold(undriven_8), .B_bus_OUT(pipeline_register_2_b_bus_out),
    .T_bus_OUT(pipeline_register_2_t_bus_out[5:0]), .CLK(CLK3), .MRyMW_IN(judge_1_reg_out[7:6]),
    .T_bus_IN(judge_1_reg_out[5:0]), .Kmx_OUT(pipeline_register_2_t_bus_out[8]));  // open: D_Address_OUT, D_Address_IN
  LED led_14 (.in(pipeline_register_viewer_4_a_is_enabled));
  Hex_Digit_Display hex_digit_display_50 (.value(pipeline_register_viewer_4_a_lsn));  // open: dp
  Hex_Digit_Display hex_digit_display_51 (.value(pipeline_register_viewer_4_a_msn));  // open: dp
  LED led_15 (.in(pipeline_register_viewer_4_b_is_enabled));
  Hex_Digit_Display hex_digit_display_52 (.value(pipeline_register_viewer_4_b_lsn));  // open: dp
  Hex_Digit_Display hex_digit_display_53 (.value(pipeline_register_viewer_4_b_msn));  // open: dp
  // NOT_Gate not_5 is placed but not wired

  // Other names for the same wires on the sheet: pulseGenManual = in_1; reg_C_address[5:0] = C_Etapa3

  // Notes on the sheet:
  //   contents of ProgramMemory (hex, n*v repeats v):
  //   800021 800042 800063 800129 80020a 200063 1000c0 200084 80c85 300029 9fffe8 400160 aaaaaa 30002a
  //   10000
  //   PC
  //   splitters que encajar con los registros de pipeline
  //   para hacer copy-paste
  //   probes que encajar en los splitters de arriba
  //   INSTRUCTION
  //   REGISTER
  //   Y USAR EL DISPLAY EN LOS PUERTOS DE SALIDA PO0 Y PO1
  //   LA IDEA ES USAR LOS DIP SWITCH EN LOS PUERTOS DE ENTRADA PI0 Y PI1
  //   ESTA CONEXION ES SOLO DE PRUEBA
  //   Detecto nueva operacion de memoria
  //   El mux es el de los is_done , el menos significativo es el de la ALU que se pone en 1 cuando termino
endmodule
