// Logisim project ALU_ALU.circ as structural Verilog: 5 circuits, main circuit ALU
module ALU (
  input  [3:0] ALUC,
  input  [15:0] A,
  input  [15:0] B,
  input  in_4,
  input  CYin,
  output [15:0] Z,
  output CYout
);

  wire and_1_out, and_2_out, and_4_out, and_5_out, aselector_1_out_4, bselector_1_out_4, CYin_t, not_1_out,
       not_2_out, not_3_out, not_4_out, not_5_out, not_6_out, not_7_out, not_8_out;
  wire [15:0] A_t, AandB, alu_full_adder_16_1_sum_out, and_3_out, AorB, B_t, CY0, CY1, notA, notB, or_1_out,
       sumAB, undriven, undriven_2, Z0, Z0xFFFF, Z1;

  not not_1 (not_1_out, ALUC[0]);
  not not_2 (not_2_out, ALUC[2]);
  not not_3 (not_3_out, ALUC[3]);
  not not_4 (not_4_out, ALUC[2]);
  not not_5 (not_5_out, ALUC[3]);
  assign CYin_t = ALUC[0] ? CYin : 1'bz;  // Controlled_Buffer controlled_buffer_1
  assign A_t = aselector_1_out_4 ? A : 16'bz;  // Controlled_Buffer controlled_buffer_2
  Aselector aselector_1 (.ALUC2(ALUC[2]), .ALUC1(ALUC[1]), .ALUC0(ALUC[0]), .out_4(aselector_1_out_4));
  and and_1 (and_1_out, not_1_out, ALUC[1], not_2_out, not_3_out);
  Bselector bselector_1 (.ALUC3(ALUC[2]), .ALUC1(ALUC[1]), .ALUC0(ALUC[0]), .out_4(bselector_1_out_4));
  assign A_t = and_1_out ? ~A : 16'bz;  // Controlled_Inverter controlled_inverter_1
  assign B_t = and_2_out ? ~B : 16'bz;  // Controlled_Inverter controlled_inverter_2
  assign B_t = bselector_1_out_4 ? B : 16'bz;  // Controlled_Buffer controlled_buffer_3
  and and_2 (and_2_out, ALUC[0], ALUC[1], not_4_out, not_5_out);
  not not_6 (not_6_out, ALUC[3]);
  not not_7 (not_7_out, ALUC[0]);
  not not_8 (not_8_out, ALUC[3]);
  assign or_1_out = A_t | B_t;  // OR_Gate or_1, 16 bits wide
  ALU_full_adder_16 alu_full_adder_16_1 (
    .Ain(A_t), .Bin(B_t), .Carryin(CYin_t), .SUM_out(alu_full_adder_16_1_sum_out), .Carry_out(CYout));
  assign and_3_out = A_t & B_t;  // AND_Gate and_3, 16 bits wide
  and and_4 (and_4_out, ALUC[0], ALUC[1], ALUC[2], not_6_out);
  and and_5 (and_5_out, not_7_out, ALUC[1], ALUC[2], not_8_out);
  assign Z = and_4_out ? ~and_3_out : 16'bz;  // Controlled_Inverter controlled_inverter_3
  assign Z = and_5_out ? ~or_1_out : 16'bz;  // Controlled_Inverter controlled_inverter_4
  assign Z = in_4 ? ~alu_full_adder_16_1_sum_out : 16'bz;  // Controlled_Inverter controlled_inverter_5
  Multiplexer #(.select(4), .width(16), .enable("false")) multiplexer_1 (
    .in0(A_t), .in1(B_t), .in2(notA), .in3(notB), .in4(undriven), .in5(sumAB), .in6(AorB), .in7(AandB),
    .in8(Z0), .in9(Z1), .in10(Z0xFFFF), .in11(CY0), .in12(CY1), .in13(undriven_2), .in14(undriven_2),
    .in15(undriven_2));  // open: out, sel
  Multiplexer #(.select(3), .width(16), .enable("false")) multiplexer_2 ();  // open: in0, in1, in2, in3, in4, in5, in6, in7, out, sel

  // Notes on the sheet:
  //   Este suma AB con Carry
endmodule

module ALU_full_adder (
  input  Xin,
  input  Yin,
  input  Cin,
  output SUMout,
  output Cout
);

  wire and_1_out, and_2_out, xor_1_out;

  xor xor_1 (xor_1_out, Xin, Yin);
  and and_1 (and_1_out, xor_1_out, Cin);
  and and_2 (and_2_out, Yin, Xin);
  xor xor_2 (SUMout, xor_1_out, Cin);
  or or_1 (Cout, and_1_out, and_2_out);
endmodule

module ALU_full_adder_16 (
  input  [15:0] Ain,
  input  [15:0] Bin,
  input  Carryin,
  output [15:0] SUM_out,
  output Carry_out
);

  wire C0, C1, C2, C3, C4, C5, C6, C7, C8, C9, C10, C11, C12, C13, C14;

  ALU_full_adder alu_full_adder_1 (.Xin(Ain[0]), .Yin(Bin[0]), .Cin(Carryin), .SUMout(SUM_out[0]), .Cout(C0));
  ALU_full_adder alu_full_adder_2 (.Xin(Ain[1]), .Yin(Bin[1]), .Cin(C0), .SUMout(SUM_out[1]), .Cout(C1));
  ALU_full_adder alu_full_adder_3 (.Xin(Ain[2]), .Yin(Bin[2]), .Cin(C1), .SUMout(SUM_out[2]), .Cout(C2));
  ALU_full_adder alu_full_adder_4 (.Xin(Ain[3]), .Yin(Bin[3]), .Cin(C2), .SUMout(SUM_out[3]), .Cout(C3));
  ALU_full_adder alu_full_adder_5 (.Xin(Ain[4]), .Yin(Bin[4]), .Cin(C3), .SUMout(SUM_out[4]), .Cout(C4));
  ALU_full_adder alu_full_adder_6 (.Xin(Ain[5]), .Yin(Bin[5]), .Cin(C4), .SUMout(SUM_out[5]), .Cout(C5));
  ALU_full_adder alu_full_adder_7 (.Xin(Ain[6]), .Yin(Bin[6]), .Cin(C5), .SUMout(SUM_out[6]), .Cout(C6));
  ALU_full_adder alu_full_adder_8 (.Xin(Ain[7]), .Yin(Bin[7]), .Cin(C6), .SUMout(SUM_out[7]), .Cout(C7));
  ALU_full_adder alu_full_adder_9 (.Xin(Ain[8]), .Yin(Bin[8]), .Cin(C7), .SUMout(SUM_out[8]), .Cout(C8));
  ALU_full_adder alu_full_adder_10 (.Xin(Ain[9]), .Yin(Bin[9]), .Cin(C8), .SUMout(SUM_out[9]), .Cout(C9));
  ALU_full_adder alu_full_adder_11 (.Xin(Ain[10]), .Yin(Bin[10]), .Cin(C9), .SUMout(SUM_out[10]), .Cout(C10));
  ALU_full_adder alu_full_adder_12 (.Xin(Ain[11]), .Yin(Bin[11]), .Cin(C10), .SUMout(SUM_out[11]), .Cout(C11));
  ALU_full_adder alu_full_adder_13 (.Xin(Ain[12]), .Yin(Bin[12]), .Cin(C11), .SUMout(SUM_out[12]), .Cout(C12));
  ALU_full_adder alu_full_adder_14 (.Xin(Ain[13]), .Yin(Bin[13]), .Cin(C12), .SUMout(SUM_out[13]), .Cout(C13));
  ALU_full_adder alu_full_adder_15 (.Xin(Ain[14]), .Yin(Bin[14]), .Cin(C13), .SUMout(SUM_out[14]), .Cout(C14));
  ALU_full_adder alu_full_adder_16 (.Xin(Ain[15]), .Yin(Bin[15]), .Cin(C14), .SUMout(SUM_out[15]), .Cout(Carry_out));

  // Other names for the same wires on the sheet: A0 = Ain[0]; A1 = Ain[1]; A2 = Ain[2]; A3 = Ain[3]; A4 = Ain[4];
  //   A5 = Ain[5]; A6 = Ain[6]; A7 = Ain[7]; A8 = Ain[8]; A9 = Ain[9]; A10 = Ain[10]; A11 = Ain[11]; A12 = Ain[12];
  //   A13 = Ain[13]; A14 = Ain[14]; A15 = Ain[15]; B0 = Bin[0]; B1 = Bin[1]; B2 = Bin[2]; B3 = Bin[3]; B4 = Bin[4];
  //   B5 = Bin[5]; B6 = Bin[6]; B7 = Bin[7]; B8 = Bin[8]; B9 = Bin[9]; B10 = Bin[10]; B11 = Bin[11]; B12 = Bin[12];
  //   B13 = Bin[13]; B14 = Bin[14]; B15 = Bin[15]; Cin = Carryin; Cout = Carry_out
endmodule

module Aselector (
  input  ALUC2,
  input  ALUC1,
  input  ALUC0,
  output out_4
);

  wire and_1_out, not_1_out, not_2_out;

  not not_1 (not_1_out, ALUC1);
  not not_2 (not_2_out, ALUC0);
  and and_1 (and_1_out, not_1_out, not_2_out);
  or or_1 (out_4, ALUC2, and_1_out);
endmodule

module Bselector (
  input  ALUC3,
  input  ALUC1,
  input  ALUC0,
  output out_4
);

  wire and_1_out, not_1_out;

  not not_1 (not_1_out, ALUC1);
  and and_1 (and_1_out, not_1_out, ALUC0);
  or or_1 (out_4, ALUC3, and_1_out);
endmodule
