// Logisim project Bloque1.circ as structural Verilog: 1 circuit, main circuit Bloque1
module Bloque1 (
  input  [15:0] register_to_test,
  input  CY,
  input  [1:0] jump_type,
  output Preload
);

  wire not_1_out, or_1_out;

  or or_1 (or_1_out, register_to_test[0], register_to_test[1], register_to_test[2], register_to_test[3], register_to_test[4], register_to_test[5], register_to_test[6], register_to_test[7], register_to_test[8], register_to_test[9], register_to_test[10], register_to_test[11], register_to_test[12], register_to_test[13], register_to_test[14], register_to_test[15]);
  not not_1 (not_1_out, or_1_out);
  Multiplexer #(.select(2), .enable("false")) multiplexer_1 (
    .in0(1'b1), .in1(not_1_out), .in2(register_to_test[15]), .in3(CY), .out(Preload), .sel(jump_type));

  // Notes on the sheet:
  //   jump type:
  //   00: jump always
  //   01: jump if carry
  //   10: jump if negative
  //   11: jump if zero
endmodule
