// Logisim project MicroInstruction_ROM.circ as structural Verilog: 1 circuit, main circuit Micro_Instruction_ROM
module Micro_Instruction_ROM (
  input  [23:0] Instruction,
  output [13:0] MicroInstruction
);

  wire [4:0] instruction_decoder_1_out_2;

  ROM #(.addrWidth(5), .dataWidth(14)) rom_1 (.addr(instruction_decoder_1_out_2), .data(MicroInstruction));
  instruction_decoder instruction_decoder_1 (.in_1(Instruction), .out_2(instruction_decoder_1_out_2));

  // Notes on the sheet:
  //   contents of rom_1 (hex, n*v repeats v):
  //   0 20 82 41 20 28 21 21 3102 0 3903 0 2103 0 91b 0 0 20 1810 2010 1803 203 403 603 281f 0 3 0 3007 0
  //   3807
endmodule
