// Logisim project PCReg.circ as structural Verilog: 1 circuit, main circuit PCreg
module PCreg (
  input  Preload,
  input  CLK1,
  input  HOLD,
  input  [10:0] B0B10,
  output [10:0] IA0IA10
);

  wire and_1_out, counter_1_carry;

  and and_1 (and_1_out, ~CLK1, ~HOLD);  // AND_Gate
  Counter #(.width(11), .max('h7ff), .ongoal("continue")) counter_1 (
    .load(Preload), .up(1'b1), .clk(and_1_out), .D(B0B10), .carry(counter_1_carry), .Q(IA0IA10));  // open: clr, count
  // also tied to GND on the sheet: counter_1_carry
endmodule
