// Logisim project PIPELINE_pipelineRegister.circ as structural Verilog: 1 circuit, main circuit Pipeline_register
module Pipeline_register (
  input  Hold,
  input  CLK,
  input  [3:0] ALUC_IN,
  input  [1:0] SH_IN,
  input  Kmx_IN,
  input  [1:0] MRyMW_IN,
  input  [5:0] A_bus_IN,
  input  [5:0] B_bus_IN,
  input  [5:0] C_bus_IN,
  input  [5:0] T_bus_IN,
  input  [9:0] D_Address_IN,
  output [3:0] ALUC_OUT,
  output [1:0] SH_OUT,
  output Kmx_OUT,
  output [1:0] MRyMW_OUT,
  output [5:0] A_bus_OUT,
  output [5:0] B_bus_OUT,
  output [5:0] C_bus_OUT,
  output [5:0] T_bus_OUT,
  output [9:0] D_Address_OUT
);

  wire not_1_out;

  not not_1 (not_1_out, Hold);
  Register #(.width(4), .trigger("falling")) ALUC (.D(ALUC_IN), .en(not_1_out), .clk(CLK), .Q(ALUC_OUT));  // open: clr
  Register #(.width(2), .trigger("falling")) SH (.D(SH_IN), .en(not_1_out), .clk(CLK), .Q(SH_OUT));  // open: clr
  Register #(.width(1), .trigger("falling")) Kmx (.D(Kmx_IN), .en(not_1_out), .clk(CLK), .Q(Kmx_OUT));  // open: clr
  Register #(.width(2), .trigger("falling")) MRyMW (
    .D(MRyMW_IN), .en(not_1_out), .clk(CLK), .Q(MRyMW_OUT));  // open: clr
  Register #(.width(6), .trigger("falling")) Abus (
    .D(A_bus_IN), .en(not_1_out), .clk(CLK), .Q(A_bus_OUT));  // open: clr
  Register #(.width(6), .trigger("falling")) Bbus (
    .D(B_bus_IN), .en(not_1_out), .clk(CLK), .Q(B_bus_OUT));  // open: clr
  Register #(.width(6), .trigger("falling")) Cbus (
    .D(C_bus_IN), .en(not_1_out), .clk(CLK), .Q(C_bus_OUT));  // open: clr
  Register #(.width(6), .trigger("falling")) Tbus (
    .D(T_bus_IN), .en(not_1_out), .clk(CLK), .Q(T_bus_OUT));  // open: clr
  Register #(.width(10), .trigger("falling")) DAddr (
    .D(D_Address_IN), .en(not_1_out), .clk(CLK), .Q(D_Address_OUT));  // open: clr
endmodule
