// Logisim project Selector_A.circ as structural Verilog: 1 circuit, main circuit Selector_A
module Selector_A (
  input  [23:0] BusB,
  output [4:0] out_2
);

  wire multiplexer_1_out;

  Multiplexer #(.select(4), .enable("false")) multiplexer_1 (
    .in0(1'b0), .in1(1'b0), .in2(1'b0), .in3(1'b1), .in4(1'b0), .in5(1'b0), .in6(1'b1), .in7(1'b1),
    .in8(1'b0), .in9(1'b0), .in10(1'b0), .in11(1'b0), .in12(1'b0), .in13(1'b0), .in14(1'b0), .in15(1'b0),
    .out(multiplexer_1_out), .sel(BusB[23:20]));
  Multiplexer #(.width(5), .enable("false")) multiplexer_2 (
    .in0(BusB[9:5]), .in1(BusB[4:0]), .out(out_2), .sel(multiplexer_1_out));
endmodule
