// Logisim project UC1.circ as structural Verilog: 1 circuit, main circuit UC1
module UC1 (
  input  [31:0] Serial_IN,
  input  [9:0] DAddress_IN,
  output ALULatchEnable,
  output ALUEnable,
  output LoadStoreEnable,
  output LoadStoreLatchEnable,
  output [31:0] Serial_ALU_OUT,
  output [31:0] Serial_Load_OUT,
  output [9:0] DAddress_ALU_OUT,
  output [9:0] DAddress_Load_OUT
);

  or or_1 (LoadStoreEnable, Serial_IN[7], Serial_IN[8]);
  not not_1 (ALUEnable, LoadStoreEnable);
  Demultiplexer #(.width(32), .enable("false")) demultiplexer_1 (
    .out0(Serial_ALU_OUT), .out1(Serial_Load_OUT), .in(Serial_IN), .sel(LoadStoreEnable));
  Demultiplexer #(.width(10), .enable("false")) demultiplexer_2 (
    .out0(DAddress_ALU_OUT), .out1(DAddress_Load_OUT), .in(DAddress_IN), .sel(LoadStoreEnable));

  assign ALULatchEnable = ALUEnable;
  assign LoadStoreLatchEnable = LoadStoreEnable;
endmodule
