// Logisim project UC2.circ as structural Verilog: 5 circuits, main circuit memory_unit_control
module memory_unit_control (
  input  set_free,
  input  set_not_free,
  input  clk,
  output is_free,
  output is_done
);

  wire counter_1_carry, not_1_out, por_1_out;

  POR #(.PorHighDuration(1)) por_1 (.out(por_1_out));
  J_K_Flip_Flop j_k_ff_1 (
    .J(set_free), .K(set_not_free), .clk(clk), .Q(is_free), .preset(por_1_out));  // open: Qn, reset
  Counter #(.width(3), .max('h6), .ongoal("stay")) counter_1 (
    .clr(is_free), .load(1'b0), .up(1'b1), .clk(clk), .carry(counter_1_carry));  // open: count, D, Q
  not not_1 (not_1_out, is_free);
  and and_1 (is_done, not_1_out, counter_1_carry);
endmodule

module UC2 (
  input  [5:0] A_etapa_1,
  input  [5:0] B_etapa_1,
  input  [5:0] C_etapa_1,
  input  [5:0] C_etapa_2_ALU,
  input  [5:0] C_etapa_2_MEM,
  input  [5:0] C_etapa_3,
  input  clk,
  output out_8
);

  dependency_detector dependency_detector_1 (
    .C_E2_ALU(C_etapa_2_ALU), .C_E1(C_etapa_1), .C_E2_MEM(C_etapa_2_MEM), .A_E1(A_etapa_1), .hold(out_8),
    .B_E1(B_etapa_1), .C_E3(C_etapa_3), .CLK(clk));
endmodule

module dependency_detector (
  input  [5:0] A_E1,
  input  [5:0] B_E1,
  input  [5:0] C_E1,
  input  [5:0] C_E2_ALU,
  input  [5:0] C_E2_MEM,
  input  [5:0] C_E3,
  input  CLK,
  output hold
);

  wire A, B, C, counter_1_carry, D, E, F, G, H, I, or_1_out;

  reg_addr_comp reg_addr_comp_1 (.equal(A), .register_2(C_E2_ALU), .register_1(A_E1));
  reg_addr_comp reg_addr_comp_2 (.equal(D), .register_2(C_E2_MEM), .register_1(A_E1));
  reg_addr_comp reg_addr_comp_3 (.equal(G), .register_2(C_E3), .register_1(A_E1));
  reg_addr_comp reg_addr_comp_4 (.equal(B), .register_2(C_E2_ALU), .register_1(B_E1));
  reg_addr_comp reg_addr_comp_5 (.equal(E), .register_2(C_E2_MEM), .register_1(B_E1));
  reg_addr_comp reg_addr_comp_6 (.equal(H), .register_2(C_E3), .register_1(B_E1));
  reg_addr_comp reg_addr_comp_7 (.equal(C), .register_2(C_E2_ALU), .register_1(C_E1));
  reg_addr_comp reg_addr_comp_8 (.equal(F), .register_2(C_E2_MEM), .register_1(C_E1));
  reg_addr_comp reg_addr_comp_9 (.equal(I), .register_2(C_E3), .register_1(C_E1));
  Counter #(.width(2), .max('h3)) counter_1 (
    .load(1'b0), .up(1'b1), .clk(CLK), .carry(counter_1_carry));  // open: clr, count, D, Q
  or or_1 (or_1_out, A, B, C, D, E, F, G, H);
  and and_1 (hold, or_1_out, counter_1_carry);
endmodule

module comparator_w_equal_disable (
  input  [4:0] operand_1,
  input  [4:0] operand_2,
  input  disable_equal_result,
  output equal
);

  wire comparator_1_eq, not_1_out;

  Comparator #(.width(5)) comparator_1 (.a(operand_1), .b(operand_2), .eq(comparator_1_eq));  // open: gt, lt
  not not_1 (not_1_out, disable_equal_result);
  and and_1 (equal, comparator_1_eq, not_1_out);

  // Notes on the sheet:
  //   Comparator of 2 operands. If disable_equal_result = 1, equal =  0. If disable_equal_result = 0, equal = 1 when operands are equal
endmodule

module reg_addr_comp (
  input  [5:0] register_1,
  input  [5:0] register_2,
  output equal
);

  wire or_1_out;

  or or_1 (or_1_out, register_1[5], register_2[5]);
  comparator_w_equal_disable comparator_w_equal_disable_1 (
    .operand_1(register_1[4:0]), .equal(equal), .operand_2(register_2[4:0]), .disable_equal_result(or_1_out));
endmodule
