// Logisim project _instruction_decoder.circ as structural Verilog: 1 circuit, main circuit instruction_decoder
module instruction_decoder (
  input  [23:0] in_1,
  output [4:0] out_2
);

  wire or_1_out;

  Multiplexer #(.width(4), .enable("false")) multiplexer_1 (
    .in0(in_1[19:16]), .in1(in_1[23:20]), .out(out_2[3:0]), .sel(or_1_out));
  or or_1 (or_1_out, in_1[20], in_1[21], in_1[22], in_1[23]);
  not not_1 (out_2[4], or_1_out);
endmodule
