// Logisim project jumpCond_.circ as structural Verilog: 1 circuit, main circuit jumpCont
module jumpCont (
  input  [5:0] T_antes,
  input  [5:0] T_despues,
  input  lo_tomo,
  output mux_selector,
  output hay_jump_en_1
);

  wire comparator_1_eq, comparator_2_eq, comparator_3_eq, comparator_4_eq, comparator_5_eq, comparator_6_eq,
       or_1_out, or_3_out;

  Comparator #(.width(6)) comparator_1 (.a(T_antes), .b(6'b101000), .eq(comparator_1_eq));  // open: gt, lt
  Comparator #(.width(6)) comparator_2 (.a(T_antes), .b(6'b100001), .eq(comparator_2_eq));  // open: gt, lt
  Comparator #(.width(6)) comparator_3 (.a(T_antes), .b(6'b100010), .eq(comparator_3_eq));  // open: gt, lt
  Comparator #(.width(6)) comparator_4 (.a(T_despues), .b(6'b101000), .eq(comparator_4_eq));  // open: gt, lt
  Comparator #(.width(6)) comparator_5 (.a(T_despues), .b(6'b100001), .eq(comparator_5_eq));  // open: gt, lt
  Comparator #(.width(6)) comparator_6 (.a(T_despues), .b(6'b100010), .eq(comparator_6_eq));  // open: gt, lt
  or or_1 (or_1_out, comparator_1_eq, comparator_2_eq, comparator_3_eq);
  or or_2 (hay_jump_en_1, comparator_4_eq, comparator_5_eq, comparator_6_eq);
  or or_3 (or_3_out, or_1_out, hay_jump_en_1);
  and and_1 (mux_selector, or_3_out, lo_tomo);
endmodule
