// Logisim project return_address_stack_.circ as structural Verilog: 1 circuit, main circuit return_address_stack
module return_address_stack (
  input  PUSH,
  input  POP,
  input  CLK,
  input  [9:0] PC,
  output [9:0] TOS
);

  wire and_1_out, and_2_out, and_3_out, j_k_ff_1_qn, or_1_out, or_2_out;
  wire [1:0] j_k_ff_1_q;

  or or_1 (or_1_out, POP, PUSH);
  and and_1 (and_1_out, or_1_out, CLK);
  J_K_Flip_Flop #(.trigger("falling")) j_k_ff_1 (
    .J(1'b1), .K(1'b1), .clk(and_1_out), .Q(j_k_ff_1_q[0]), .Qn(j_k_ff_1_qn));  // open: preset, reset
  and and_2 (and_2_out, PUSH, j_k_ff_1_q[0]);
  and and_3 (and_3_out, j_k_ff_1_qn, ~PUSH);  // AND_Gate
  J_K_Flip_Flop #(.trigger("falling")) j_k_ff_2 (
    .J(or_2_out), .K(or_2_out), .clk(and_1_out), .Q(j_k_ff_1_q[1]));  // open: Qn, preset, reset
  or or_2 (or_2_out, and_2_out, and_3_out);
  RAM #(.addrWidth(2), .dataWidth(10), .databus("bibus")) ram_1 (
    .addr(j_k_ff_1_q), .we(PUSH), .oe(POP), .clk(CLK), .din(PC), .dout(TOS));

  // Notes on the sheet:
  //   enable
  //   b0
  //   b1
endmodule
