// Logisim project viewers.circ as structural Verilog: 4 circuits, main circuit pipeline_register_viewer
module pipeline_register_viewer (
  input  [14:0] microinstruction,
  input  [5:0] A_in,
  input  [5:0] B_in,
  input  [5:0] C_in,
  output [3:0] b16,
  output [3:0] b15,
  output [3:0] b14,
  output [3:0] b13,
  output [3:0] b12,
  output [3:0] b11,
  output [3:0] b10,
  output [3:0] b9,
  output [3:0] b8,
  output [3:0] b7,
  output [3:0] b6,
  output [3:0] b5,
  output [3:0] b4,
  output [3:0] b3,
  output [3:0] b2,
  output [3:0] b1,
  output [3:0] b0,
  output A_is_enabled,
  output [3:0] A_MSN,
  output [3:0] A_LSN,
  output B_is_enabled,
  output [3:0] B_MSN,
  output [3:0] B_LSN,
  output C_is_enabled,
  output [3:0] C_MSN,
  output [3:0] C_LSN
);

  wire comparator_1_eq, comparator_2_eq, comparator_3_eq, comparator_4_eq, comparator_5_eq, comparator_6_eq,
       comparator_7_eq, comparator_8_eq, comparator_9_eq, comparator_10_eq, comparator_11_eq,
       comparator_12_eq, comparator_13_eq, comparator_14_eq, comparator_15_eq, comparator_16_eq,
       comparator_17_eq, comparator_18_eq, comparator_19_eq, comparator_20_eq, comparator_21_eq,
       comparator_22_eq, comparator_23_eq;
  wire [19:0] undriven, undriven_2, undriven_3;

  Comparator #(.width(15)) comparator_1 (.a(15'h102), .b(microinstruction), .eq(comparator_1_eq));  // open: gt, lt
  Comparator #(.width(15)) comparator_2 (.a(15'h3903), .b(microinstruction), .eq(comparator_2_eq));  // open: gt, lt
  Comparator #(.width(15)) comparator_3 (.a(15'h3103), .b(microinstruction), .eq(comparator_3_eq));  // open: gt, lt
  Comparator #(.width(15)) comparator_4 (.a(15'h291b), .b(microinstruction), .eq(comparator_4_eq));  // open: gt, lt
  Comparator #(.width(15)) comparator_5 (.a(15'h20), .b(microinstruction), .eq(comparator_5_eq));  // open: gt, lt
  Comparator #(.width(15)) comparator_6 (.a(15'h28), .b(microinstruction), .eq(comparator_6_eq));  // open: gt, lt
  Comparator #(.width(15)) comparator_7 (.a(15'h21), .b(microinstruction), .eq(comparator_7_eq));  // open: gt, lt
  Comparator #(.width(15)) comparator_8 (.a(15'h21), .eq(comparator_8_eq));  // open: b, gt, lt
  Comparator #(.width(15)) comparator_9 (.a(15'h82), .b(microinstruction), .eq(comparator_9_eq));  // open: gt, lt
  Comparator #(.width(15)) comparator_10 (.a(15'h41), .b(microinstruction), .eq(comparator_10_eq));  // open: gt, lt
  Comparator #(.width(15)) comparator_11 (.a(15'h20), .eq(comparator_11_eq));  // open: b, gt, lt
  Comparator #(.width(15)) comparator_12 (.a(15'h281f), .b(microinstruction), .eq(comparator_12_eq));  // open: gt, lt
  Comparator #(.width(15)) comparator_13 (.a(15'h3), .b(microinstruction), .eq(comparator_13_eq));  // open: gt, lt
  Comparator #(.width(15)) comparator_14 (.a(15'h3007), .b(microinstruction), .eq(comparator_14_eq));  // open: gt, lt
  Comparator #(.width(15)) comparator_15 (.a(15'h3807), .b(microinstruction), .eq(comparator_15_eq));  // open: gt, lt
  Comparator #(.width(15)) comparator_16 (.a(15'h1803), .b(microinstruction), .eq(comparator_16_eq));  // open: gt, lt
  Comparator #(.width(15)) comparator_17 (.a(15'h203), .b(microinstruction), .eq(comparator_17_eq));  // open: gt, lt
  Comparator #(.width(15)) comparator_18 (.a(15'h403), .b(microinstruction), .eq(comparator_18_eq));  // open: gt, lt
  Comparator #(.width(15)) comparator_19 (.a(15'h603), .b(microinstruction), .eq(comparator_19_eq));  // open: gt, lt
  Comparator #(.width(15)) comparator_20 (.a(15'h5810), .b(microinstruction), .eq(comparator_20_eq));  // open: gt, lt
  Comparator #(.width(15)) comparator_21 (.a(15'h6010), .b(microinstruction), .eq(comparator_21_eq));  // open: gt, lt
  Comparator #(.width(15)) comparator_22 (.a(15'h20), .eq(comparator_22_eq));  // open: b, gt, lt
  Comparator #(.width(15)) comparator_23 (.a({15{1'b0}}), .b(microinstruction), .eq(comparator_23_eq));  // open: gt, lt
  assign {b4, b3, b2, b1, b0} = comparator_1_eq ? 20'hf44a9 : 20'bz;  // Controlled_Buffer controlled_buffer_1
  assign {b10, b9, b8, b7, b6} = comparator_1_eq ? 20'h69996 : 20'bz;  // Controlled_Buffer controlled_buffer_2
  assign {b4, b3, b2, b1, b0} = comparator_2_eq ? 20'hf44a9 : 20'bz;  // Controlled_Buffer controlled_buffer_3
  assign {b10, b9, b8, b7, b6} = comparator_2_eq ? 20'hf842f : 20'bz;  // Controlled_Buffer controlled_buffer_4
  assign {b10, b9, b8, b7, b6} = comparator_3_eq ? 20'hfaaa5 : 20'bz;  // Controlled_Buffer controlled_buffer_5
  assign {b4, b3, b2, b1, b0} = comparator_3_eq ? 20'hf44a9 : 20'bz;  // Controlled_Buffer controlled_buffer_6
  assign {b4, b3, b2, b1, b0} = comparator_4_eq ? 20'hf44a9 : 20'bz;  // Controlled_Buffer controlled_buffer_7
  assign {b10, b9, b8, b7, b6} = comparator_4_eq ? 20'hf9996 : 20'bz;  // Controlled_Buffer controlled_buffer_8
  assign {b4, b3, b2, b1, b0} = comparator_5_eq ? 20'hfaaa4 : 20'bz;  // Controlled_Buffer controlled_buffer_9
  assign {b10, b9, b8, b7, b6} = comparator_5_eq ? 20'hf424f : 20'bz;  // Controlled_Buffer controlled_buffer_10
  assign {b10, b9, b8, b7, b6} = comparator_6_eq ? 20'h69999 : 20'bz;  // Controlled_Buffer controlled_buffer_11
  assign {b4, b3, b2, b1, b0} = comparator_6_eq ? 20'h69999 : 20'bz;  // Controlled_Buffer controlled_buffer_12
  assign {b10, b9, b8, b7, b6} = comparator_7_eq ? 20'hf842f : 20'bz;  // Controlled_Buffer controlled_buffer_13
  assign {b4, b3, b2, b1, b0} = comparator_7_eq ? 20'h69bd1 : 20'bz;  // Controlled_Buffer controlled_buffer_14
  Controlled_Buffer #(.width(20)) controlled_buffer_15 (.in(20'h69bd1), .en(comparator_8_eq));  // open: out
  Controlled_Buffer #(.width(20)) controlled_buffer_16 (.in(20'h9bd9), .en(comparator_8_eq));  // open: out
  assign {b10, b9, b8, b7, b6} = comparator_9_eq ? 20'h69996 : 20'bz;  // Controlled_Buffer controlled_buffer_17
  assign {b4, b3, b2, b1, b0} = comparator_9_eq ? 20'hf424f : 20'bz;  // Controlled_Buffer controlled_buffer_18
  assign {b4, b3, b2, b1, b0} = comparator_10_eq ? 20'hf424f : 20'bz;  // Controlled_Buffer controlled_buffer_19
  assign {b10, b9, b8, b7, b6} = comparator_10_eq ? 20'h69996 : 20'bz;  // Controlled_Buffer controlled_buffer_20
  Controlled_Buffer #(.width(20)) controlled_buffer_21 (.in(undriven_3), .en(comparator_11_eq));  // open: out
  Controlled_Buffer #(.width(20)) controlled_buffer_22 (.in(undriven_2), .en(comparator_11_eq));  // open: out
  assign {b10, b9, b8, b7, b6} = comparator_12_eq ? 20'hf9996 : 20'bz;  // Controlled_Buffer controlled_buffer_23
  assign {b4, b3, b2, b1, b0} = comparator_12_eq ? 20'hfaaa5 : 20'bz;  // Controlled_Buffer controlled_buffer_24
  assign {b4, b3, b2, b1, b0} = comparator_13_eq ? 20'hc212c : 20'bz;  // Controlled_Buffer controlled_buffer_25
  assign {b10, b9, b8, b7, b6} = comparator_13_eq ? 20'h69996 : 20'bz;  // Controlled_Buffer controlled_buffer_26
  assign {b10, b9, b8, b7, b6} = comparator_14_eq ? 20'hfaaa5 : 20'bz;  // Controlled_Buffer controlled_buffer_27
  assign {b4, b3, b2, b1, b0} = comparator_14_eq ? 20'hfaaa5 : 20'bz;  // Controlled_Buffer controlled_buffer_28
  assign {b10, b9, b8, b7, b6} = comparator_15_eq ? 20'hf842f : 20'bz;  // Controlled_Buffer controlled_buffer_29
  assign {b4, b3, b2, b1, b0} = comparator_15_eq ? 20'hfaaa5 : 20'bz;  // Controlled_Buffer controlled_buffer_30
  assign {b4, b3, b2, b1, b0} = comparator_16_eq ? 20'hf1111 : 20'bz;  // Controlled_Buffer controlled_buffer_31
  assign {b10, b9, b8, b7, b6} = comparator_16_eq ? 20'hfaaa4 : 20'bz;  // Controlled_Buffer controlled_buffer_32
  assign {b10, b9, b8, b7, b6} = comparator_17_eq ? 20'h1db8 : 20'bz;  // Controlled_Buffer controlled_buffer_33
  assign {b4, b3, b2, b1, b0} = comparator_17_eq ? 20'hfaaa5 : 20'bz;  // Controlled_Buffer controlled_buffer_34
  assign {b4, b3, b2, b1, b0} = comparator_18_eq ? 20'hf1111 : 20'bz;  // Controlled_Buffer controlled_buffer_35
  assign {b10, b9, b8, b7, b6} = comparator_18_eq ? 20'h1db8 : 20'bz;  // Controlled_Buffer controlled_buffer_36
  assign {b4, b3, b2, b1, b0} = comparator_19_eq ? 20'hfaaa5 : 20'bz;  // Controlled_Buffer controlled_buffer_37
  assign {b10, b9, b8, b7, b6} = comparator_19_eq ? 20'h1db8 : 20'bz;  // Controlled_Buffer controlled_buffer_38
  assign {b4, b3, b2, b1, b0} = comparator_20_eq ? 20'hfaaa5 : 20'bz;  // Controlled_Buffer controlled_buffer_39
  assign {b10, b9, b8, b7, b6} = comparator_20_eq ? 20'hf1111 : 20'bz;  // Controlled_Buffer controlled_buffer_40
  assign {b4, b3, b2, b1, b0} = comparator_21_eq ? 20'h88f88 : 20'bz;  // Controlled_Buffer controlled_buffer_41
  assign {b10, b9, b8, b7, b6} = comparator_21_eq ? 20'h69bd1 : 20'bz;  // Controlled_Buffer controlled_buffer_42
  Controlled_Buffer #(.width(20)) controlled_buffer_43 (.in(20'h69bd1));  // open: out, en
  Controlled_Buffer #(.width(20)) controlled_buffer_44 (.in(20'h88f88), .en(comparator_22_eq));  // open: out
  assign {b4, b3, b2, b1, b0} = comparator_23_eq ? {20{1'b1}} : 20'bz;  // Controlled_Buffer controlled_buffer_45
  assign {b10, b9, b8, b7, b6} = comparator_23_eq ? {20{1'b1}} : 20'bz;  // Controlled_Buffer controlled_buffer_46
  assign {b16, b15, b14, b13, b12} = comparator_1_eq ? 20'hf424f : 20'bz;  // Controlled_Buffer controlled_buffer_47
  assign {b16, b15, b14, b13, b12} = comparator_2_eq ? 20'h36a63 : 20'bz;  // Controlled_Buffer controlled_buffer_48
  assign {b16, b15, b14, b13, b12} = comparator_3_eq ? 20'h69996 : 20'bz;  // Controlled_Buffer controlled_buffer_49
  assign {b16, b15, b14, b13, b12} = comparator_4_eq ? 20'h36a63 : 20'bz;  // Controlled_Buffer controlled_buffer_50
  assign {b16, b15, b14, b13, b12} = comparator_5_eq ? 20'h2999e : 20'bz;  // Controlled_Buffer controlled_buffer_51
  assign {b16, b15, b14, b13, b12} = comparator_6_eq ? 20'h2999e : 20'bz;  // Controlled_Buffer controlled_buffer_52
  assign {b16, b15, b14, b13, b12} = comparator_7_eq ? 20'h2999e : 20'bz;  // Controlled_Buffer controlled_buffer_53
  Controlled_Buffer #(.width(20)) controlled_buffer_54 (.in(20'h2999e));  // open: out, en
  assign {b16, b15, b14, b13, b12} = comparator_9_eq ? 20'hf424f : 20'bz;  // Controlled_Buffer controlled_buffer_55
  assign {b16, b15, b14, b13, b12} = comparator_10_eq ? 20'hf424f : 20'bz;  // Controlled_Buffer controlled_buffer_56
  Controlled_Buffer #(.width(20)) controlled_buffer_57 (.in(undriven), .en(comparator_11_eq));  // open: out
  assign {b16, b15, b14, b13, b12} = comparator_12_eq ? 20'h36a63 : 20'bz;  // Controlled_Buffer controlled_buffer_58
  assign {b16, b15, b14, b13, b12} = comparator_13_eq ? 20'hf424f : 20'bz;  // Controlled_Buffer controlled_buffer_59
  assign {b16, b15, b14, b13, b12} = comparator_14_eq ? 20'h69996 : 20'bz;  // Controlled_Buffer controlled_buffer_60
  assign {b16, b15, b14, b13, b12} = comparator_15_eq ? 20'h36a63 : 20'bz;  // Controlled_Buffer controlled_buffer_61
  assign {b16, b15, b14, b13, b12} = comparator_16_eq ? 20'h69999 : 20'bz;  // Controlled_Buffer controlled_buffer_62
  assign {b16, b15, b14, b13, b12} = comparator_17_eq ? 20'h36a63 : 20'bz;  // Controlled_Buffer controlled_buffer_63
  assign {b16, b15, b14, b13, b12} = comparator_18_eq ? 20'hf1111 : 20'bz;  // Controlled_Buffer controlled_buffer_64
  assign {b16, b15, b14, b13, b12} = comparator_19_eq ? 20'hf1111 : 20'bz;  // Controlled_Buffer controlled_buffer_65
  assign {b16, b15, b14, b13, b12} = comparator_20_eq ? 20'h69999 : 20'bz;  // Controlled_Buffer controlled_buffer_66
  assign {b16, b15, b14, b13, b12} = comparator_21_eq ? 20'h1db8 : 20'bz;  // Controlled_Buffer controlled_buffer_67
  Controlled_Buffer #(.width(20)) controlled_buffer_68 (.in(20'hfaaa5));  // open: out, en
  assign {b16, b15, b14, b13, b12} = comparator_23_eq ? {20{1'b1}} : 20'bz;  // Controlled_Buffer controlled_buffer_69
  not not_1 (A_MSN[2], A_in[5]);
  not not_2 (B_MSN[2], B_in[5]);
  not not_3 (C_MSN[2], C_in[5]);

  assign A_is_enabled = A_in[5];
  assign A_LSN = A_in[3:0];
  assign {A_MSN[3], A_MSN[1:0]} = {A_in[4], {2{A_MSN[2]}}};
  assign b5 = 4'b0000;
  assign b11 = 4'b0000;
  assign B_is_enabled = B_in[5];
  assign B_LSN = B_in[3:0];
  assign {B_MSN[3], B_MSN[1:0]} = {B_in[4], {2{B_MSN[2]}}};
  assign C_is_enabled = C_in[5];
  assign C_LSN = C_in[3:0];
  assign {C_MSN[3], C_MSN[1:0]} = {C_in[4], {2{C_MSN[2]}}};

  // Notes on the sheet:
  //   A
  //   B
  //   C
  //   D
  //   E
  //   J
  //   K
  //   L
  //   M
  //   N
  //   O
  //   P
  //   R
  //   S
  //   T
  //   V
  //   Y
  //   Z
  //   MOK
  //   ANK
  //   ORK
  //   ADK
  //   JMP
  //   JCY
  //   JNE
  //   JZE
  //   MOM
  //   MOM
  //   BSR
  //   ADR
  //   MOV
  //   ORR
  //   ANR
  //   CPL
  //   ASR
  //   LSL
  //   LSR
  //   CLR
  //   SET
  //   RET
  //   RET
  //   M
  //   O
  //   K
  //   A
  //   N
  //   K
  //   O
  //   R
  //   K
  //   A
  //   D
  //   K
  //   J
  //   M
  //   P
  //   J
  //   C
  //   Y
  //   J
  //   N
  //   E
  //   J
  //   Z
  //   E
  //   M
  //   O
  //   M
  //   M
  //   O
  //   M
  //   A
  //   D
  //   R
  //   M
  //   O
  //   V
  //   O
  //   R
  //   R
  //   A
  //   N
  //   R
  //   C
  //   P
  //   L
  //   A
  //   S
  //   R
  //   L
  //   S
  //   L
  //   L
  //   S
  //   R
  //   C
  //   L
  //   R
  //   S
  //   E
  //   T
  //   R
  //   E
  //   T
endmodule

module register_bank_viewer (
  input  [5:0] A_data_out,
  input  [15:0] A_address,
  input  [5:0] B_data_out,
  input  [15:0] B_address,
  input  [5:0] C_data_out,
  input  [15:0] C_address,
  output A_is_enabled,
  output [3:0] A_data_MSN,
  output [3:0] A_data_LSN,
  output [3:0] A_address_N3,
  output [3:0] A_address_N2,
  output [3:0] A_address_N1,
  output [3:0] A_address_N0,
  output B_is_enabled,
  output [3:0] B_data_MSN,
  output [3:0] B_data_LSN,
  output [3:0] B_address_N3,
  output [3:0] B_address_N2,
  output [3:0] B_address_N1,
  output [3:0] B_address_N0,
  output C_is_enabled,
  output [3:0] C_data_MSN,
  output [3:0] C_data_LSN,
  output [3:0] C_address_N3,
  output [3:0] C_address_N2,
  output [3:0] C_address_N1,
  output [3:0] C_address_N0
);

  not not_1 (A_data_MSN[2], A_data_out[5]);
  not not_2 (B_data_MSN[2], B_data_out[5]);
  not not_3 (C_data_MSN[2], C_data_out[5]);

  assign A_address_N0 = A_address[3:0];
  assign A_address_N1 = A_address[7:4];
  assign A_address_N2 = A_address[11:8];
  assign A_address_N3 = A_address[15:12];
  assign A_data_LSN = A_data_out[3:0];
  assign {A_data_MSN[3], A_data_MSN[1:0]} = {A_data_out[4], {2{A_data_MSN[2]}}};
  assign A_is_enabled = A_data_out[5];
  assign B_address_N0 = B_address[3:0];
  assign B_address_N1 = B_address[7:4];
  assign B_address_N2 = B_address[11:8];
  assign B_address_N3 = B_address[15:12];
  assign B_data_LSN = B_data_out[3:0];
  assign {B_data_MSN[3], B_data_MSN[1:0]} = {B_data_out[4], {2{B_data_MSN[2]}}};
  assign B_is_enabled = B_data_out[5];
  assign C_address_N0 = C_address[3:0];
  assign C_address_N1 = C_address[7:4];
  assign C_address_N2 = C_address[11:8];
  assign C_address_N3 = C_address[15:12];
  assign C_data_LSN = C_data_out[3:0];
  assign {C_data_MSN[3], C_data_MSN[1:0]} = {C_data_out[4], {2{C_data_MSN[2]}}};
  assign C_is_enabled = C_data_out[5];
endmodule

module UC2_viewer (
  input  hold,
  output [7:0] out_2,
  output [7:0] out_3,
  output [7:0] out_4,
  output [7:0] out_5,
  output [7:0] out_6,
  output [7:0] out_7,
  output [7:0] out_8,
  output [7:0] out_9
);

  Multiplexer #(.width(8), .enable("false")) multiplexer_1 (.in0({8{1'b0}}), .in1(8'h3c), .out(out_2), .sel(hold));
  Multiplexer #(.width(8), .enable("false")) multiplexer_2 (.in0({8{1'b0}}), .in1(8'h42), .out(out_3), .sel(hold));
  Multiplexer #(.width(8), .enable("false")) multiplexer_3 (.in0({8{1'b0}}), .in1(8'h85), .out(out_4), .sel(hold));
  Multiplexer #(.width(8), .enable("false")) multiplexer_4 (.in0({8{1'b0}}), .in1(8'h89), .out(out_5), .sel(hold));
  Multiplexer #(.width(8), .enable("false")) multiplexer_5 (.in0({8{1'b0}}), .in1(8'h91), .out(out_6), .sel(hold));
  Multiplexer #(.width(8), .enable("false")) multiplexer_6 (.in0({8{1'b0}}), .in1(8'ha1), .out(out_7), .sel(hold));
  Multiplexer #(.width(8), .enable("false")) multiplexer_7 (.in0({8{1'b0}}), .in1(8'h42), .out(out_8), .sel(hold));
  Multiplexer #(.width(8), .enable("false")) multiplexer_8 (.in0({8{1'b0}}), .in1(8'h3c), .out(out_9), .sel(hold));
endmodule

module clk_edge_viewer (
  input  in_1,
  output [7:0] out_2,
  output [7:0] out_3,
  output [7:0] out_4,
  output [7:0] out_5,
  output [7:0] out_6,
  output [7:0] out_7,
  output [7:0] out_8,
  output [7:0] out_9
);

  Multiplexer #(.width(8), .enable("false")) multiplexer_1 (.in0(8'h80), .in1(8'h1), .out(out_2), .sel(in_1));
  Multiplexer #(.width(8), .enable("false")) multiplexer_2 (.in0(8'ha0), .in1(8'h9), .out(out_3), .sel(in_1));
  Multiplexer #(.width(8), .enable("false")) multiplexer_3 (.in0(8'h90), .in1(8'h11), .out(out_4), .sel(in_1));
  Multiplexer #(.width(8), .enable("false")) multiplexer_4 (.in0({8{1'b1}}), .in1({8{1'b1}}), .out(out_5), .sel(in_1));
  Multiplexer #(.width(8), .enable("false")) multiplexer_5 (.in0(8'h11), .in1(8'h90), .out(out_6), .sel(in_1));
  Multiplexer #(.width(8), .enable("false")) multiplexer_6 (.in0(8'h21), .in1(8'h88), .out(out_7), .sel(in_1));
  Multiplexer #(.width(8), .enable("false")) multiplexer_7 (.in0(8'h1), .in1(8'h80), .out(out_8), .sel(in_1));
  Multiplexer #(.width(8), .enable("false")) multiplexer_8 (.in0(8'h1), .in1(8'h80), .out(out_9), .sel(in_1));
endmodule
